// Logisim project 16-Bit Computer.circ as structural Verilog
module main (
  input  RES,
  input  ENABLE
);

  wire _7f_RES_out, alu_1_mod_reg0, alu_func_mux_1_ena, alu_func_mux_1_enb, alu_func_mux_1_wsela,
       alu_func_mux_1_wselb, alu_func_mux_1_y_mux, CLK_out, cu_condition_unit_1_ccen_2,
       cu_condition_unit_1_ovf, cu_condition_unit_1_sgn, cu_condition_unit_1_zero, display_controler_1_neg,
       ff_RES_out, ram_register_1_clk_2, \µir_1_a0 , \µir_1_a1 , \µir_1_a2 , \µir_1_a3 , \µir_1_asel ,
       \µir_1_asel_2 , \µir_1_b0 , \µir_1_b1 , \µir_1_b2 , \µir_1_b3 , \µir_1_bsel , \µir_1_bsel_2 ,
       \µir_1_ccen , \µir_1_ccen_2 , \µir_1_cond_0 , \µir_1_cond_1 , \µir_1_cond_2 , \µir_1_cond_3 ,
       \µir_1_const15 , \µir_1_const_0 , \µir_1_const_1 , \µir_1_const_2 , \µir_1_const_3 , \µir_1_const_4 ,
       \µir_1_const_5 , \µir_1_const_6 , \µir_1_const_7 , \µir_1_const_8 , \µir_1_const_9 , \µir_1_const_10 ,
       \µir_1_const_11 , \µir_1_const_12 , \µir_1_const_13 , \µir_1_const_14 , \µir_1_cs , \µir_1_cs_2 ,
       \µir_1_disp , \µir_1_func_0 , \µir_1_func_1 , \µir_1_func_2 , \µir_1_func_3 , \µir_1_func_4 ,
       \µir_1_func_5 , \µir_1_ir_ld , \µir_1_ir_ld_2 , \µir_1_ir_res , \µir_1_ir_res_2 , \µir_1_kmux ,
       \µir_1_kmux_2 , \µir_1_numdsp , \µir_1_pc_bus_0 , \µir_1_pc_bus_1 , \µir_1_pc_inc , \µir_1_pc_inc_2 ,
       \µir_1_pc_ld , \µir_1_pc_ld_2 , \µir_1_rb0 , \µir_1_rb1 , \µir_1_rb2 , \µir_1_rd , \µir_1_rd_2 ,
       \µir_1_shift_0 , \µir_1_shift_1 , \µir_1_shift_2 , \µir_1_shift_3 , \µir_1_shift_4 , \µir_1_shift_5 ,
       \µir_1_ssel0 , \µir_1_ssel2 , \µir_1_ssel_1 , \µir_1_stack_0 , \µir_1_stack_1 , \µir_1_stack_2 ,
       \µir_1_ymux , \µir_1_ymux_2 , \µir_1_µd0 , \µir_1_µd1 , \µir_1_µd2 , \µir_1_µd3 , \µir_1_µd4 ,
       \µir_1_µd5 , \µir_1_µd6 , \µir_1_µd7 , \µir_1_µd8 , \µir_1_µd9 , \µir_1_µd10 , \µir_1_µd11 ,
       \µir_1_µd12 , \µir_1_µd13 , \µir_1_µd14 , \µir_1_µd15 , \µir_1_µdsel , \µir_1_µdsel_2 ,
       \µir_1_µir_sel0 , \µir_1_µir_sel1 , \µir_1_µsr , \µir_1_µsr_2 ;
  wire [1:0] \µir_1_pc_bus , \µir_1_µir_sel ;
  wire [2:0] alu_1_ovf, alu_v2_shifter_1_out_b_2, \µir_1_reg_bus , \µir_1_ssel , \µir_1_stack ;
  wire [3:0] A_out_13, alu_func_mux_1_f0, alu_v2_shifter_1_out_b, alu_v2_shifter_1_out_b_4,
       alu_v2_shifter_1_out_b_5, B_out_13, display_controler_1_o3_0, display_controler_1_o7_4,
       display_controler_1_o11_8, display_controler_1_o15_12, ir_instruction_register_1__3_0,
       ir_instruction_register_1__7_4, ir_instruction_register_1__11_8, ir_instruction_register_1__15_12,
       multiplexer_1_out, multiplexer_2_out, ram_register_1_ebp_15_8, ram_register_1_ebp_15_8_2,
       ram_register_1_esp_15_8, ram_register_1_esp_15_8_2, \µir_1_areg , \µir_1_breg , \µir_1_cond ;
  wire [3:3] alu_v2_shifter_1_out_b_3;
  wire [5:0] \µir_1_func , \µir_1_shift ;
  wire [7:0] \cu_control_unit_1_µprog , ram_register_1_ebp_7_0, ram_register_1_esp_7_0;
  wire [15:0] alu_1_mod, alu_1_output, alu_input_mux_1_l, alu_input_mux_1_r, alu_k_mux_1_k_input,
       alu_reg_a_mux_1_bus_output_a, alu_reg_a_mux_1_bus_output_b, alu_reg_a_mux_1_output,
       alu_reg_b_mux_1_bus_output, alu_reg_b_mux_1_output, alu_y_mux_1_abus, alu_y_mux_1_dbus,
       cu_control_unit_1_mps, ir_instruction_register_1_ireg, Program_Counter_q, ram_register_1_abus,
       ram_register_1_dbus, \µir_1_const , \µir_1_µir_data ;
  wire [31:0] \cu_µcs_1_µir_1 , \cu_µcs_1_µir_2 , \cu_µcs_1_µir_3 ;

  Clock CLK (.out(CLK_out));
  LED led_1 (.in(\µir_1_cs_2 ));
  LED led_2 (.in(\µir_1_stack_2 ));
  LED led_3 (.in(\µir_1_rd_2 ));
  LED led_4 (.in(\µir_1_stack_0 ));
  LED led_5 (.in(\µir_1_stack_1 ));
  LED led_6 (.in(\µir_1_pc_ld_2 ));
  Hex_Digit_Display hex_digit_display_1 (.value(ram_register_1_dbus[15:12]));  // open: dp
  Hex_Digit_Display hex_digit_display_2 (.value(ram_register_1_esp_15_8_2));  // open: dp
  Hex_Digit_Display hex_digit_display_3 (.value(ram_register_1_ebp_15_8_2));  // open: dp
  Button ff_RES (.out(ff_RES_out));
  Button _7f_RES (.out(_7f_RES_out));
  \µIR  \u_µir_1  (
    .\µIR_IN_1 (\cu_µcs_1_µir_1 ), .\µIR_IN_2 (\cu_µcs_1_µir_2 ), .\µIR_IN_3 (\cu_µcs_1_µir_3 ),
    .CS(\µir_1_cs ), .CLK(CLK_out), .CS_2(\µir_1_cs_2 ), .PC_INC(\µir_1_pc_inc ), .PC_BUS(\µir_1_pc_bus ),
    .IR_LD(\µir_1_ir_ld ), .IR_RES(\µir_1_ir_res ), .YMUX(\µir_1_ymux ), .NUMDSP(\µir_1_numdsp ),
    .DISP(\µir_1_disp ), .CONST(\µir_1_const ), .YMUX_2(\µir_1_ymux_2 ), .PC_INC_2(\µir_1_pc_inc_2 ),
    .PC_BUS_1(\µir_1_pc_bus_1 ), .IR_LD_2(\µir_1_ir_ld_2 ), .IR_RES_2(\µir_1_ir_res_2 ),
    .\µDSEL_2 (\µir_1_µdsel_2 ), .CONST_14(\µir_1_const_14 ), .CONST_12(\µir_1_const_12 ),
    .CONST_10(\µir_1_const_10 ), .CONST_8(\µir_1_const_8 ), .CONST_6(\µir_1_const_6 ),
    .CONST_4(\µir_1_const_4 ), .CONST_2(\µir_1_const_2 ), .CONST_0(\µir_1_const_0 ),
    .CONST15(\µir_1_const15 ), .CONST_13(\µir_1_const_13 ), .CONST_11(\µir_1_const_11 ),
    .CONST_9(\µir_1_const_9 ), .CONST_7(\µir_1_const_7 ), .CONST_5(\µir_1_const_5 ),
    .CONST_3(\µir_1_const_3 ), .CONST_1(\µir_1_const_1 ), .STACK(\µir_1_stack ), .RD(\µir_1_rd ),
    .RD_2(\µir_1_rd_2 ), .STACK_0(\µir_1_stack_0 ), .STACK_1(\µir_1_stack_1 ), .STACK_2(\µir_1_stack_2 ),
    .PC_LD(\µir_1_pc_ld ), .PC_LD_2(\µir_1_pc_ld_2 ), .\µIR_SEL (\µir_1_µir_sel ),
    .\µIR_SEL0 (\µir_1_µir_sel0 ), .\µIR_SEL1 (\µir_1_µir_sel1 ), .\µDSEL (\µir_1_µdsel ),
    .\µIR_DATA (\µir_1_µir_data ), .\µD14 (\µir_1_µd14 ), .\µD12 (\µir_1_µd12 ), .\µD10 (\µir_1_µd10 ),
    .\µD8 (\µir_1_µd8 ), .\µD6 (\µir_1_µd6 ), .\µD4 (\µir_1_µd4 ), .\µD2 (\µir_1_µd2 ), .\µD0 (\µir_1_µd0 ),
    .\µD15 (\µir_1_µd15 ), .\µD13 (\µir_1_µd13 ), .\µD11 (\µir_1_µd11 ), .\µD9 (\µir_1_µd9 ),
    .\µD7 (\µir_1_µd7 ), .\µD5 (\µir_1_µd5 ), .\µD3 (\µir_1_µd3 ), .\µD1 (\µir_1_µd1 ), .CCEN(\µir_1_ccen ),
    .\µSR (\µir_1_µsr ), .COND(\µir_1_cond ), .ASEL(\µir_1_asel ), .COND_3(\µir_1_cond_3 ),
    .COND_0(\µir_1_cond_0 ), .CCEN_2(\µir_1_ccen_2 ), .\µSR_2 (\µir_1_µsr_2 ), .ASEL_2(\µir_1_asel_2 ),
    .COND_2(\µir_1_cond_2 ), .COND_1(\µir_1_cond_1 ), .AREG(\µir_1_areg ), .BSEL(\µir_1_bsel ),
    .A3(\µir_1_a3 ), .A0(\µir_1_a0 ), .BSEL_2(\µir_1_bsel_2 ), .A2(\µir_1_a2 ), .A1(\µir_1_a1 ),
    .BREG(\µir_1_breg ), .SSEL(\µir_1_ssel ), .FUNC(\µir_1_func ), .KMUX(\µir_1_kmux ), .B3(\µir_1_b3 ),
    .B0(\µir_1_b0 ), .SSEL2(\µir_1_ssel2 ), .SSEL0(\µir_1_ssel0 ), .FUNC_5(\µir_1_func_5 ),
    .FUNC_1(\µir_1_func_1 ), .KMUX_2(\µir_1_kmux_2 ), .FUNC_3(\µir_1_func_3 ), .B2(\µir_1_b2 ),
    .B1(\µir_1_b1 ), .SSEL_1(\µir_1_ssel_1 ), .FUNC_4(\µir_1_func_4 ), .FUNC_2(\µir_1_func_2 ),
    .REG_BUS(\µir_1_reg_bus ), .RB2(\µir_1_rb2 ), .RB0(\µir_1_rb0 ), .RB1(\µir_1_rb1 ),
    .PC_BUS_0(\µir_1_pc_bus_0 ), .FUNC_0(\µir_1_func_0 ), .SHIFT(\µir_1_shift ), .SHIFT_5(\µir_1_shift_5 ),
    .SHIFT_1(\µir_1_shift_1 ), .SHIFT_3(\µir_1_shift_3 ), .SHIFT_0(\µir_1_shift_0 ),
    .SHIFT_4(\µir_1_shift_4 ), .SHIFT_2(\µir_1_shift_2 ));
  LED led_7 (.in(\µir_1_pc_bus_0 ));
  LED led_8 (.in(\µir_1_pc_inc_2 ));
  LED led_9 (.in(\µir_1_pc_bus_1 ));
  Hex_Digit_Display hex_digit_display_4 (.value(ram_register_1_dbus[11:8]));  // open: dp
  Hex_Digit_Display hex_digit_display_5 (.value(ram_register_1_esp_15_8));  // open: dp
  Hex_Digit_Display hex_digit_display_6 (.value(ram_register_1_ebp_15_8));  // open: dp
  RAM_Register ram_register_1 (
    .INPUT(ram_register_1_dbus), .ABUS(ram_register_1_abus), .DBUS(ram_register_1_dbus),
    .RAM_REG(\µir_1_stack ), .CLK_2(ram_register_1_clk_2),
    .EBP_15_8({ram_register_1_ebp_15_8_2, ram_register_1_ebp_15_8}), .EBP_7_0(ram_register_1_ebp_7_0),
    .ESP_15_8({ram_register_1_esp_15_8_2, ram_register_1_esp_15_8}), .ESP_7_0(ram_register_1_esp_7_0),
    .CLK(CLK_out), .ff_RES(ff_RES_out), ._7f_RES(_7f_RES_out));
  LED led_10 (.in(\µir_1_ir_res_2 ));
  LED led_11 (.in(\µir_1_ir_ld_2 ));
  RAM #(.addrWidth(16), .dataWidth(16)) ram_1 (
    .addr(ram_register_1_abus), .data(ram_register_1_dbus), .sel(\µir_1_cs ), .clk(ram_register_1_clk_2),
    .ld(\µir_1_rd ));  // open: clr
  Hex_Digit_Display hex_digit_display_7 (.value(ram_register_1_dbus[3:0]));  // open: dp
  Hex_Digit_Display hex_digit_display_8 (.value(ram_register_1_dbus[7:4]));  // open: dp
  Hex_Digit_Display hex_digit_display_9 (.value(ram_register_1_esp_7_0[3:0]));  // open: dp
  Hex_Digit_Display hex_digit_display_10 (.value(ram_register_1_esp_7_0[7:4]));  // open: dp
  Hex_Digit_Display hex_digit_display_11 (.value(ram_register_1_ebp_7_0[3:0]));  // open: dp
  Hex_Digit_Display hex_digit_display_12 (.value(ram_register_1_ebp_7_0[7:4]));  // open: dp
  LED led_12 (.in(\µir_1_µir_sel0 ));
  LED led_13 (.in(\µir_1_µdsel_2 ));
  LED led_14 (.in(\µir_1_µir_sel1 ));
  LED led_15 (.in(\µir_1_µd15 ));
  LED led_16 (.in(\µir_1_µd12 ));
  LED led_17 (.in(\µir_1_µd14 ));
  LED led_18 (.in(\µir_1_µd13 ));
  Counter #(.width(16), .max('hffff)) Program_Counter (
    .load(\µir_1_pc_ld ), .D(ram_register_1_dbus), .count(\µir_1_pc_inc ), .Q(Program_Counter_q),
    .clk(CLK_out), .clr(RES));  // open: carry
  LED led_19 (.in(\µir_1_µd10 ));
  LED led_20 (.in(\µir_1_µd11 ));
  LED led_21 (.in(\µir_1_µd9 ));
  LED led_22 (.in(\µir_1_µd8 ));
  PC_Controler pc_controler_1 (
    .PC_IN(Program_Counter_q), .ENB_OUT(\µir_1_pc_bus [1]), .DBUS(ram_register_1_dbus),
    .ABUS(ram_register_1_abus), .BUS_SEL(\µir_1_pc_bus [0]));
  LED led_23 (.in(\µir_1_µd6 ));
  LED led_24 (.in(\µir_1_µd4 ));
  LED led_25 (.in(\µir_1_µd7 ));
  LED led_26 (.in(\µir_1_µd5 ));
  LED led_27 (.in(\µir_1_µd3 ));
  LED led_28 (.in(\µir_1_µd0 ));
  LED led_29 (.in(\µir_1_µd2 ));
  LED led_30 (.in(\µir_1_µd1 ));
  Hex_Digit_Display hex_digit_display_13 (.value(ir_instruction_register_1__15_12));  // open: dp
  LED led_31 (.in(\µir_1_ccen_2 ));
  LED led_32 (.in(\µir_1_µsr_2 ));
  IR_Instruction_Register ir_instruction_register_1 (
    .IR_LD(\µir_1_ir_ld ), .CLK(CLK_out), .IR_RES(\µir_1_ir_res ), .DBUS(ram_register_1_dbus),
    .IREG(ir_instruction_register_1_ireg), ._15_12(ir_instruction_register_1__15_12),
    ._11_8(ir_instruction_register_1__11_8), ._7_4(ir_instruction_register_1__7_4),
    ._3_0(ir_instruction_register_1__3_0));
  Hex_Digit_Display hex_digit_display_14 (.value(ir_instruction_register_1__11_8));  // open: dp
  \CU_µCS  \cu_µcs_1  (
    .\µAddress (cu_control_unit_1_mps), .MPS_ENABLE(ENABLE), .\µIR_1 (\cu_µcs_1_µir_1 ),
    .\µIR_2 (\cu_µcs_1_µir_2 ), .\µIR_3 (\cu_µcs_1_µir_3 ));
  LED led_33 (.in(\µir_1_cond_1 ));
  LED led_34 (.in(\µir_1_cond_3 ));
  LED led_35 (.in(\µir_1_cond_2 ));
  LED led_36 (.in(\µir_1_cond_0 ));
  Hex_Digit_Display hex_digit_display_15 (.value(ir_instruction_register_1__3_0));  // open: dp
  Hex_Digit_Display hex_digit_display_16 (.value(ir_instruction_register_1__7_4));  // open: dp
  CU_Control_Unit cu_control_unit_1 (
    .BUS_ADDRESS(ir_instruction_register_1_ireg[15:8]), .ENB(ENABLE), .DSEL(\µir_1_µdsel ), .CLK(CLK_out),
    .CCEN(cu_condition_unit_1_ccen_2), .ADDRSSEL(\µir_1_µir_sel ), .MPS(cu_control_unit_1_mps),
    .CONST(\µir_1_µir_data ), .\µPROG (\cu_control_unit_1_µprog ));
  LED led_37 (.in(\µir_1_a3 ));
  LED led_38 (.in(\µir_1_asel_2 ));
  LED led_39 (.in(\µir_1_a2 ));
  Hex_Digit_Display hex_digit_display_17 (.value(\cu_control_unit_1_µprog [7:4]));  // open: dp
  Hex_Digit_Display hex_digit_display_18 (.value(\cu_control_unit_1_µprog [3:0]));  // open: dp
  LED led_40 (.in(\µir_1_a1 ));
  LED led_41 (.in(\µir_1_a0 ));
  ALU_XA_MUX A (
    .MUX(\µir_1_asel ), .in_1(ir_instruction_register_1_ireg[7]), .in_2(ir_instruction_register_1_ireg[6]),
    .in_3(ir_instruction_register_1_ireg[5]), .in_4(ir_instruction_register_1_ireg[4]),
    .in_5(\µir_1_areg [3]), .in_6(\µir_1_areg [2]), .in_7(\µir_1_areg [1]), .in_8(\µir_1_areg [0]),
    .out_10(A_out_13[3]), .out_11(A_out_13[2]), .out_12(A_out_13[1]), .out_13(A_out_13[0]));
  REG_BUS_Controler reg_bus_controler_1 (
    .BUS_SEL(\µir_1_reg_bus [1]), .ENB_OUT(\µir_1_reg_bus [2]), .REGA(alu_reg_a_mux_1_bus_output_a),
    .REGB(alu_reg_a_mux_1_bus_output_b), .DBUS(ram_register_1_dbus), .ABUS(ram_register_1_abus),
    .REG_SEL(\µir_1_reg_bus [0]));
  LED led_42 (.in(\µir_1_bsel_2 ));
  LED led_43 (.in(\µir_1_b2 ));
  LED led_44 (.in(\µir_1_b3 ));
  LED led_45 (.in(\µir_1_b1 ));
  LED ZERO (.in(cu_condition_unit_1_zero));
  LED SGN (.in(cu_condition_unit_1_sgn));
  LED OVF (.in(cu_condition_unit_1_ovf));
  LED led_46 (.in(\µir_1_ssel2 ));
  LED led_47 (.in(\µir_1_b0 ));
  LED led_48 (.in(\µir_1_ssel_1 ));
  ALU_XB_MUX B (
    .MUX(\µir_1_bsel ), .in_1(ir_instruction_register_1_ireg[3]), .in_2(ir_instruction_register_1_ireg[2]),
    .in_3(ir_instruction_register_1_ireg[1]), .in_4(ir_instruction_register_1_ireg[0]),
    .in_5(\µir_1_breg [3]), .in_6(\µir_1_breg [2]), .in_7(\µir_1_breg [1]), .in_8(\µir_1_breg [0]),
    .out_10(B_out_13[3]), .out_11(B_out_13[2]), .out_12(B_out_13[1]), .out_13(B_out_13[0]));
  LED led_49 (.in(\µir_1_ssel0 ));
  LED led_50 (.in(\µir_1_func_5 ));
  Multiplexer #(.width(4), .enable("false")) multiplexer_1 (
    .in0(4'b0000), .in1(A_out_13), .out(multiplexer_1_out), .sel(alu_func_mux_1_wsela));
  CU_Condition_Unit cu_condition_unit_1 (
    .FLAGS(alu_1_ovf), .CLK(CLK_out), .\µSR_ENABLE (\µir_1_µsr ), .CCEN_2(cu_condition_unit_1_ccen_2),
    .FLAG_SEL(\µir_1_cond ), .SGN(cu_condition_unit_1_sgn), .ZERO(cu_condition_unit_1_zero),
    .OVF(cu_condition_unit_1_ovf), .CCEN(\µir_1_ccen ));
  LED led_51 (.in(\µir_1_func_4 ));
  LED led_52 (.in(\µir_1_func_2 ));
  LED led_53 (.in(\µir_1_func_3 ));
  LED led_54 (.in(\µir_1_func_1 ));
  LED led_55 (.in(\µir_1_kmux_2 ));
  LED led_56 (.in(\µir_1_func_0 ));
  TTY #(.cols(40)) tty_1 (
    .data({alu_v2_shifter_1_out_b_2, alu_v2_shifter_1_out_b}), .clk(CLK_out), .we(\µir_1_disp ));  // open: clr
  Display_Controler display_controler_1 (
    .NEG(display_controler_1_neg), .I15_12(alu_v2_shifter_1_out_b_5),
    .I7_4({alu_v2_shifter_1_out_b_3[3], alu_v2_shifter_1_out_b_2}), .O7_4(display_controler_1_o7_4),
    .DISPLAY_ENABLE(\µir_1_numdsp ), .I11_8(alu_v2_shifter_1_out_b_4), .I3_0(alu_v2_shifter_1_out_b),
    .O11_8(display_controler_1_o11_8), .O15_12(display_controler_1_o15_12), .O3_0(display_controler_1_o3_0));
  LED led_57 (.in(\µir_1_const_14 ));
  LED led_58 (.in(\µir_1_const_13 ));
  LED led_59 (.in(\µir_1_const15 ));
  _7_Segment_Display u_7_segment_display_1 (.g(display_controler_1_neg));  // open: f, a, b, e, d, c, dp
  Hex_Digit_Display hex_digit_display_19 (.value(display_controler_1_o15_12));  // open: dp
  ALU_REG_A_MUX alu_reg_a_mux_1 (
    .CLK(CLK_out), .Output(alu_reg_a_mux_1_output), .WSEL(multiplexer_1_out), .RSEL(A_out_13),
    .Data({alu_v2_shifter_1_out_b_5, alu_v2_shifter_1_out_b_4, alu_v2_shifter_1_out_b_3[3], alu_v2_shifter_1_out_b_2, alu_v2_shifter_1_out_b}),
    .BUS_INPUT_B(alu_reg_b_mux_1_bus_output), .BUS_Output_A(alu_reg_a_mux_1_bus_output_a),
    .BUS_Output_B(alu_reg_a_mux_1_bus_output_b));
  ALU_FUNC_MUX alu_func_mux_1 (
    .WSELA(alu_func_mux_1_wsela), .WSELB(alu_func_mux_1_wselb), .Y_MUX(alu_func_mux_1_y_mux),
    .F2(alu_func_mux_1_f0[2]), .F1(alu_func_mux_1_f0[1]), .F0(alu_func_mux_1_f0[0]),
    .ENA(alu_func_mux_1_ena), .ENB(alu_func_mux_1_enb), .FUNC(\µir_1_func ), .F3(alu_func_mux_1_f0[3]));
  LED led_60 (.in(\µir_1_const_9 ));
  LED led_61 (.in(\µir_1_const_12 ));
  LED led_62 (.in(\µir_1_const_10 ));
  LED led_63 (.in(\µir_1_const_11 ));
  Hex_Digit_Display hex_digit_display_20 (.value(display_controler_1_o11_8));  // open: dp
  Hex_Digit_Display hex_digit_display_21 (.value(display_controler_1_o7_4));  // open: dp
  ALU_K_MUX alu_k_mux_1 (
    .in_3(\µir_1_kmux ), .DATABUS(ram_register_1_dbus), .CONST(\µir_1_const ), .K_INPUT(alu_k_mux_1_k_input));
  ALU_Input_MUX alu_input_mux_1 (
    .AREG(alu_reg_a_mux_1_output), .DATA(alu_k_mux_1_k_input), .SEL(\µir_1_ssel ), .ZERO({16{1'b0}}),
    .BREG(alu_reg_b_mux_1_output), .L(alu_input_mux_1_l), .R(alu_input_mux_1_r));
  ALU alu_1 (
    ._15(alu_input_mux_1_l[15]), ._14(alu_input_mux_1_l[14]), ._13(alu_input_mux_1_l[13]),
    ._12(alu_input_mux_1_l[12]), ._11(alu_input_mux_1_l[11]), ._10(alu_input_mux_1_l[10]),
    ._9(alu_input_mux_1_l[9]), ._8(alu_input_mux_1_l[8]), ._7(alu_input_mux_1_l[7]),
    ._6(alu_input_mux_1_l[6]), ._5(alu_input_mux_1_l[5]), ._4(alu_input_mux_1_l[4]),
    ._3(alu_input_mux_1_l[3]), ._2(alu_input_mux_1_l[2]), ._1(alu_input_mux_1_l[1]),
    ._0(alu_input_mux_1_l[0]), ._15_2(alu_input_mux_1_r[15]), ._14_2(alu_input_mux_1_r[14]),
    ._13_2(alu_input_mux_1_r[13]), ._12_2(alu_input_mux_1_r[12]), ._11_2(alu_input_mux_1_r[11]),
    ._10_2(alu_input_mux_1_r[10]), ._9_2(alu_input_mux_1_r[9]), ._8_2(alu_input_mux_1_r[8]),
    ._7_2(alu_input_mux_1_r[7]), ._6_2(alu_input_mux_1_r[6]), ._5_2(alu_input_mux_1_r[5]),
    ._4_2(alu_input_mux_1_r[4]), ._3_2(alu_input_mux_1_r[3]), ._2_2(alu_input_mux_1_r[2]),
    ._1_2(alu_input_mux_1_r[1]), ._0_2(alu_input_mux_1_r[0]), .F0(alu_func_mux_1_f0[0]),
    .F1(alu_func_mux_1_f0[1]), .F2(alu_func_mux_1_f0[2]), .ENA(alu_func_mux_1_ena), .ENB(alu_func_mux_1_enb),
    .SGN(alu_1_ovf[2]), .ZERO(alu_1_ovf[1]), .OVF(alu_1_ovf[0]), .OUTPUT(alu_1_output), .MOD(alu_1_mod),
    .MOD_REG0(alu_1_mod_reg0), .F3(alu_func_mux_1_f0[3]));
  LED led_64 (.in(\µir_1_const_8 ));
  LED led_65 (.in(\µir_1_const_5 ));
  LED led_66 (.in(\µir_1_const_7 ));
  LED led_67 (.in(\µir_1_const_6 ));
  Hex_Digit_Display hex_digit_display_22 (.value(display_controler_1_o3_0));  // open: dp
  ALU_REG_B_MUX alu_reg_b_mux_1 (
    .CLK(CLK_out), .Output(alu_reg_b_mux_1_output), .WSEL(multiplexer_2_out), .RSEL(B_out_13),
    .Data({alu_v2_shifter_1_out_b_5, alu_v2_shifter_1_out_b_4, alu_v2_shifter_1_out_b_3[3], alu_v2_shifter_1_out_b_2, alu_v2_shifter_1_out_b}),
    .MOD(alu_1_mod), .BUS_Output(alu_reg_b_mux_1_bus_output), .MOD_REG0_ENB(alu_1_mod_reg0));
  LED led_68 (.in(\µir_1_const_4 ));
  LED led_69 (.in(\µir_1_const_2 ));
  LED led_70 (.in(\µir_1_const_1 ));
  LED led_71 (.in(\µir_1_const_3 ));
  assign ram_register_1_dbus = alu_y_mux_1_dbus;  // Buffer buffer_1, 16 bits wide
  LED led_72 (.in(\µir_1_rb1 ));
  LED led_73 (.in(\µir_1_rb2 ));
  LED led_74 (.in(\µir_1_const_0 ));
  assign ram_register_1_abus = alu_y_mux_1_abus;  // Buffer buffer_2, 16 bits wide
  ALU_Y_MUX alu_y_mux_1 (
    .BUS_SEL(\µir_1_ymux ), .ENB_SEL(alu_func_mux_1_y_mux), .DBUS(alu_y_mux_1_dbus), .ABUS(alu_y_mux_1_abus),
    .DATA({alu_v2_shifter_1_out_b_5, alu_v2_shifter_1_out_b_4, alu_v2_shifter_1_out_b_3[3], alu_v2_shifter_1_out_b_2, alu_v2_shifter_1_out_b}),
    .CLK(CLK_out));
  Multiplexer #(.width(4), .enable("false")) multiplexer_2 (
    .in0(4'b0000), .in1(B_out_13), .out(multiplexer_2_out), .sel(alu_func_mux_1_wselb));
  ALU_v2_SHIFTER alu_v2_shifter_1 (
    .OUT_B({alu_v2_shifter_1_out_b_5, alu_v2_shifter_1_out_b_4, alu_v2_shifter_1_out_b_3[3], alu_v2_shifter_1_out_b_2, alu_v2_shifter_1_out_b}),
    .IN_A(alu_1_output), .SHIFT(\µir_1_shift ));
  LED led_75 (.in(\µir_1_rb0 ));
  LED led_76 (.in(\µir_1_ymux_2 ));
  LED led_77 (.in(\µir_1_shift_5 ));
  LED led_78 (.in(\µir_1_shift_4 ));
  LED led_79 (.in(\µir_1_shift_3 ));
  LED led_80 (.in(\µir_1_shift_0 ));
  LED led_81 (.in(\µir_1_shift_1 ));
  LED led_82 (.in(\µir_1_shift_2 ));

  // Notes on the sheet:
  //   µPROG
endmodule

module \µIR  (
  input  [31:0] \µIR_IN_1 ,
  input  [31:0] \µIR_IN_2 ,
  input  CLK,
  input  [31:0] \µIR_IN_3 ,
  output CS,
  output [2:0] STACK,
  output RD,
  output PC_LD,
  output PC_INC,
  output [1:0] PC_BUS,
  output IR_LD,
  output IR_RES,
  output [1:0] \µIR_SEL ,
  output \µDSEL ,
  output CCEN,
  output \µSR ,
  output [3:0] COND,
  output ASEL,
  output [3:0] AREG,
  output BSEL,
  output [3:0] BREG,
  output [2:0] SSEL,
  output [5:0] FUNC,
  output KMUX,
  output YMUX,
  output [2:0] REG_BUS,
  output [5:0] SHIFT,
  output NUMDSP,
  output DISP,
  output [15:0] \µIR_DATA ,
  output [15:0] CONST,
  output \µIR_SEL0 ,
  output \µD14 ,
  output \µD12 ,
  output \µD10 ,
  output \µD8 ,
  output \µD6 ,
  output \µD4 ,
  output \µD2 ,
  output \µD0 ,
  output COND_3,
  output COND_0,
  output YMUX_2,
  output RB2,
  output RB0,
  output CS_2,
  output STACK_2,
  output STACK_0,
  output RD_2,
  output PC_LD_2,
  output PC_INC_2,
  output PC_BUS_1,
  output PC_BUS_0,
  output IR_LD_2,
  output IR_RES_2,
  output \µIR_SEL1 ,
  output \µDSEL_2 ,
  output \µD15 ,
  output \µD13 ,
  output \µD11 ,
  output \µD9 ,
  output \µD7 ,
  output \µD5 ,
  output \µD3 ,
  output \µD1 ,
  output CCEN_2,
  output \µSR_2 ,
  output ASEL_2,
  output A3,
  output A0,
  output BSEL_2,
  output B3,
  output B0,
  output SSEL2,
  output SSEL0,
  output FUNC_5,
  output FUNC_1,
  output KMUX_2,
  output SHIFT_5,
  output SHIFT_1,
  output STACK_1,
  output COND_2,
  output COND_1,
  output FUNC_3,
  output FUNC_0,
  output RB1,
  output SHIFT_3,
  output SHIFT_0,
  output A2,
  output A1,
  output B2,
  output B1,
  output SSEL_1,
  output FUNC_4,
  output FUNC_2,
  output SHIFT_4,
  output SHIFT_2,
  output CONST_14,
  output CONST_12,
  output CONST_10,
  output CONST_8,
  output CONST_6,
  output CONST_4,
  output CONST_2,
  output CONST_0,
  output CONST15,
  output CONST_13,
  output CONST_11,
  output CONST_9,
  output CONST_7,
  output CONST_5,
  output CONST_3,
  output CONST_1
);

  wire [11:0] \µIR_3_q ;

  Register #(.width(32)) \u_µIR_1  (
    .D(\µIR_IN_1 ),
    .Q({CS, STACK, RD, PC_LD, PC_INC, PC_BUS, IR_LD, IR_RES, \µIR_SEL , \µDSEL , \µD15 , \µD14 , \µD13 , \µD12 , \µD11 , \µD10 , \µD9 , \µD8 , \µD7 , \µD6 , \µD5 , \µD4 , \µD3 , \µD2 , \µD1 , \µD0 , CCEN, \µSR }),
    .clk(CLK));  // open: en, clr
  Register #(.width(32)) \u_µIR_2  (
    .D(\µIR_IN_2 ), .Q({COND, ASEL, A3, A2, A1, A0, BSEL, B3, B2, B1, B0, SSEL, FUNC, KMUX, CONST[15:8]}),
    .clk(CLK));  // open: en, clr
  Register #(.width(32)) \u_µIR_3  (
    .D(\µIR_IN_3 ), .Q({CONST[7:0], YMUX, RB2, RB1, RB0, SHIFT, NUMDSP, DISP, \µIR_3_q }), .clk(CLK));  // open: en, clr

  assign AREG = {A3, A2, A1, A0};
  assign ASEL_2 = ASEL;
  assign BREG = {B3, B2, B1, B0};
  assign BSEL_2 = BSEL;
  assign CCEN_2 = CCEN;
  assign COND_0 = COND[0];
  assign COND_1 = COND[1];
  assign COND_2 = COND[2];
  assign COND_3 = COND[3];
  assign CONST15 = CONST[15];
  assign CONST_0 = CONST[0];
  assign CONST_1 = CONST[1];
  assign CONST_2 = CONST[2];
  assign CONST_3 = CONST[3];
  assign CONST_4 = CONST[4];
  assign CONST_5 = CONST[5];
  assign CONST_6 = CONST[6];
  assign CONST_7 = CONST[7];
  assign CONST_8 = CONST[8];
  assign CONST_9 = CONST[9];
  assign CONST_10 = CONST[10];
  assign CONST_11 = CONST[11];
  assign CONST_12 = CONST[12];
  assign CONST_13 = CONST[13];
  assign CONST_14 = CONST[14];
  assign CS_2 = CS;
  assign FUNC_0 = FUNC[0];
  assign FUNC_1 = FUNC[1];
  assign FUNC_2 = FUNC[2];
  assign FUNC_3 = FUNC[3];
  assign FUNC_4 = FUNC[4];
  assign FUNC_5 = FUNC[5];
  assign IR_LD_2 = IR_LD;
  assign IR_RES_2 = IR_RES;
  assign KMUX_2 = KMUX;
  assign PC_BUS_0 = PC_BUS[0];
  assign PC_BUS_1 = PC_BUS[1];
  assign PC_INC_2 = PC_INC;
  assign PC_LD_2 = PC_LD;
  assign RD_2 = RD;
  assign REG_BUS = {RB2, RB1, RB0};
  assign SHIFT_0 = SHIFT[0];
  assign SHIFT_1 = SHIFT[1];
  assign SHIFT_2 = SHIFT[2];
  assign SHIFT_3 = SHIFT[3];
  assign SHIFT_4 = SHIFT[4];
  assign SHIFT_5 = SHIFT[5];
  assign SSEL0 = SSEL[0];
  assign SSEL2 = SSEL[2];
  assign SSEL_1 = SSEL[1];
  assign STACK_0 = STACK[0];
  assign STACK_1 = STACK[1];
  assign STACK_2 = STACK[2];
  assign YMUX_2 = YMUX;
  assign \µDSEL_2  = \µDSEL ;
  assign \µIR_DATA  = {\µD15 , \µD14 , \µD13 , \µD12 , \µD11 , \µD10 , \µD9 , \µD8 , \µD7 , \µD6 , \µD5 , \µD4 , \µD3 , \µD2 , \µD1 , \µD0 };
  assign \µIR_SEL0  = \µIR_SEL [0];
  assign \µIR_SEL1  = \µIR_SEL [1];
  assign \µSR_2  = \µSR ;
endmodule

// DISPLAY
module Display_Controler (
  input  [3:0] I15_12,
  input  [3:0] I7_4,
  input  DISPLAY_ENABLE,
  input  [3:0] I11_8,
  input  [3:0] I3_0,
  output NEG,
  output [3:0] O15_12,
  output [3:0] O7_4,
  output [3:0] O11_8,
  output [3:0] O3_0
);

  wire adder_2_cout, adder_3_cout, adder_4_cout;
  wire [3:0] adder_1_out, adder_2_out, adder_3_out, adder_4_out, multiplexer_1_out, multiplexer_2_out,
       multiplexer_3_out, multiplexer_4_out, not_1_out, not_2_out, not_3_out, not_4_out, transistor_1_out,
       transistor_2_out, transistor_3_out, transistor_4_out;
  wire [7:0] rom_1_data, rom_2_data, rom_3_data, rom_4_data;

  Register #(.width(1), .trigger("falling")) register_1 (
    .D(I15_12[3]), .Q(NEG), .clk(DISPLAY_ENABLE));  // open: en, clr
  assign not_1_out = ~I15_12;  // NOT_Gate not_1, 4 bits wide
  assign not_2_out = ~I11_8;  // NOT_Gate not_2, 4 bits wide
  Adder #(.width(4)) adder_1 (.a(4'b0000), .b(not_1_out), .out(adder_1_out), .cin(adder_2_cout));  // open: cout
  Adder #(.width(4)) adder_2 (.a(4'b0000), .b(not_2_out), .out(adder_2_out), .cin(adder_3_cout), .cout(adder_2_cout));
  ROM #(.addrWidth(4)) rom_1 (.addr(I15_12), .data(rom_1_data), .sel(DISPLAY_ENABLE));
  Multiplexer #(.width(4), .enable("false")) multiplexer_1 (
    .in0(I15_12), .in1(adder_1_out), .out(multiplexer_1_out), .sel(I15_12[3]));
  Transistor #(.\type ("n"), .gate("br"), .width(4)) transistor_1 (
    .in(multiplexer_1_out), .out(transistor_1_out), .gate(DISPLAY_ENABLE));
  ROM #(.addrWidth(4)) rom_2 (.addr(I11_8), .data(rom_2_data), .sel(DISPLAY_ENABLE));
  Transistor #(.\type ("n"), .gate("br"), .width(4)) transistor_2 (
    .in(multiplexer_2_out), .out(transistor_2_out), .gate(DISPLAY_ENABLE));
  Multiplexer #(.width(4), .enable("false")) multiplexer_2 (
    .in0(I11_8), .in1(adder_2_out), .out(multiplexer_2_out), .sel(I15_12[3]));
  Register #(.width(4), .trigger("falling")) register_2 (
    .D(transistor_1_out), .Q(O15_12), .clk(DISPLAY_ENABLE));  // open: en, clr
  Register #(.width(4), .trigger("falling")) register_3 (
    .D(transistor_2_out), .Q(O11_8), .clk(DISPLAY_ENABLE));  // open: en, clr
  LED led_1 (.in(rom_1_data[0]));
  LED led_2 (.in(rom_1_data[2]));
  LED led_3 (.in(rom_1_data[1]));
  LED led_4 (.in(rom_1_data[3]));
  LED led_5 (.in(rom_1_data[7]));
  LED led_6 (.in(rom_1_data[5]));
  LED led_7 (.in(rom_1_data[4]));
  LED led_8 (.in(rom_1_data[6]));
  LED led_9 (.in(rom_2_data[3]));
  LED led_10 (.in(rom_2_data[2]));
  LED led_11 (.in(rom_2_data[1]));
  LED led_12 (.in(rom_2_data[0]));
  LED led_13 (.in(rom_2_data[4]));
  LED led_14 (.in(rom_2_data[5]));
  LED led_15 (.in(rom_2_data[7]));
  LED led_16 (.in(rom_2_data[6]));
  assign not_3_out = ~I7_4;  // NOT_Gate not_3, 4 bits wide
  assign not_4_out = ~I3_0;  // NOT_Gate not_4, 4 bits wide
  ROM #(.addrWidth(4)) rom_3 (.addr(I7_4), .data(rom_3_data), .sel(DISPLAY_ENABLE));
  Multiplexer #(.width(4), .enable("false")) multiplexer_3 (
    .in0(I7_4), .in1(adder_3_out), .out(multiplexer_3_out), .sel(I15_12[3]));
  Adder #(.width(4)) adder_3 (.a(4'b0000), .b(not_3_out), .out(adder_3_out), .cin(adder_4_cout), .cout(adder_3_cout));
  ROM #(.addrWidth(4)) rom_4 (.addr(I3_0), .data(rom_4_data), .sel(DISPLAY_ENABLE));
  Multiplexer #(.width(4), .enable("false")) multiplexer_4 (
    .in0(I3_0), .in1(adder_4_out), .out(multiplexer_4_out), .sel(I15_12[3]));
  Adder #(.width(4)) adder_4 (.a(4'b0001), .b(not_4_out), .out(adder_4_out), .cout(adder_4_cout));  // open: cin
  Transistor #(.\type ("n"), .gate("br"), .width(4)) transistor_3 (
    .in(multiplexer_3_out), .out(transistor_3_out), .gate(DISPLAY_ENABLE));
  Register #(.width(4), .trigger("falling")) register_4 (
    .D(transistor_3_out), .Q(O7_4), .clk(DISPLAY_ENABLE));  // open: en, clr
  Transistor #(.\type ("n"), .gate("br"), .width(4)) transistor_4 (
    .in(multiplexer_4_out), .out(transistor_4_out), .gate(DISPLAY_ENABLE));
  Register #(.width(4), .trigger("falling")) register_5 (
    .D(transistor_4_out), .Q(O3_0), .clk(DISPLAY_ENABLE));  // open: en, clr
  LED led_17 (.in(rom_3_data[1]));
  LED led_18 (.in(rom_3_data[0]));
  LED led_19 (.in(rom_3_data[2]));
  LED led_20 (.in(rom_3_data[4]));
  LED led_21 (.in(rom_3_data[5]));
  LED led_22 (.in(rom_3_data[6]));
  LED led_23 (.in(rom_4_data[1]));
  LED led_24 (.in(rom_4_data[2]));
  LED led_25 (.in(rom_4_data[0]));
  LED led_26 (.in(rom_4_data[6]));
  LED led_27 (.in(rom_4_data[4]));
  LED led_28 (.in(rom_4_data[5]));
  LED led_29 (.in(rom_3_data[3]));
  LED led_30 (.in(rom_3_data[7]));
  LED led_31 (.in(rom_4_data[3]));
  LED led_32 (.in(rom_4_data[7]));

  // Notes on the sheet:
  //   0 = CC
  //   1 = LU
  //   2 = CU
  //   3 = RU
  //   contents of rom_1 (hex, n*v repeats v):
  //   7e 48 3d 6d 4b 67 77 4c 7f 6f 5f 73 36 79 37 17
  //   4 = LD
  //   5 = CD
  //   6 = RD
  //   7 = PP
  //   0 = CC
  //   1 = LU
  //   2 = CU
  //   3 = RU
  //   contents of rom_2 (hex, n*v repeats v):
  //   7e 48 3d 6d 4b 67 77 4c 7f 6f 5f 73 36 79 37 17
  //   4 = LD
  //   5 = CD
  //   6 = RD
  //   7 = PP
  //   1 = LU
  //   contents of rom_3 (hex, n*v repeats v):
  //   7e 48 3d 6d 4b 67 77 4c 7f 6f 5f 73 36 79 37 17
  //   4 = LD
  //   7 = PP
  //   1 = LU
  //   contents of rom_4 (hex, n*v repeats v):
  //   7e 48 3d 6d 4b 67 77 4c 7f 6f 5f 73 36 79 37 17
  //   4 = LD
  //   7 = PP
  //   0 = CC
  //   2 = CU
  //   3 = RU
  //   5 = CD
  //   6 = RD
  //   0 = CC
  //   2 = CU
  //   3 = RU
  //   5 = CD
  //   6 = RD
endmodule

module ALU (
  input  _15,
  input  _14,
  input  _13,
  input  _12,
  input  _11,
  input  _10,
  input  _9,
  input  _8,
  input  _7,
  input  _6,
  input  _5,
  input  _4,
  input  _3,
  input  _2,
  input  _1,
  input  _0,
  input  _15_2,
  input  _14_2,
  input  _13_2,
  input  _12_2,
  input  _11_2,
  input  _10_2,
  input  _9_2,
  input  _8_2,
  input  _7_2,
  input  _6_2,
  input  _5_2,
  input  _4_2,
  input  _3_2,
  input  _2_2,
  input  _1_2,
  input  _0_2,
  input  ENA,
  input  ENB,
  input  F0,
  input  F1,
  input  F2,
  input  F3,
  output [15:0] MOD,
  output MOD_REG0,
  output [15:0] OUTPUT,
  output SGN,
  output ZERO,
  output OVF
);

  wire alu_f_fun_mux_1_fa0, alu_f_fun_mux_1_fa1, alu_f_fun_mux_1_sub, n16_bit_alu_1_carry;
  wire [2:0] alu_div_1_ovf, alu_mul_1_ovf, alu_nop_block_1_ovf, alu_xor_1_ovf, n16_bit_alu_1_ovf;
  wire [15:0] alu_div_1_div_output, alu_div_1_mod, alu_mul_1_output, alu_nop_block_1_out, alu_xor_1_out_xor,
       n16_bit_alu_1_o0;

  ALU_NOP_BLOCK alu_nop_block_1 (
    .ENA(ENA), .ENB(ENB), .SGN(alu_nop_block_1_ovf[2]), .ZERO(alu_nop_block_1_ovf[1]),
    .IN_A({_15, _14, _13, _12, _11, _10, _9, _8, _7, _6, _5, _4, _3, _2, _1, _0}),
    .IN_B({_15_2, _14_2, _13_2, _12_2, _11_2, _10_2, _9_2, _8_2, _7_2, _6_2, _5_2, _4_2, _3_2, _2_2, _1_2, _0_2}),
    .OUT(alu_nop_block_1_out), .OVF(alu_nop_block_1_ovf[0]));
  ALU_F_FUN_MUX alu_f_fun_mux_1 (
    .SUB(alu_f_fun_mux_1_sub), .FA1(alu_f_fun_mux_1_fa1), .FA0(alu_f_fun_mux_1_fa0), .F2(F2), .F1(F1), .F0(F0));
  _16_Bit_ALU u_16_bit_alu_1 (
    ._15(_15), ._14(_14), ._13(_13), ._12(_12), ._11(_11), ._10(_10), ._9(_9), ._8(_8), ._7(_7), ._6(_6),
    ._5(_5), ._4(_4), ._3(_3), ._2(_2), ._1(_1), ._0(_0), ._15_2(_15_2), ._14_2(_14_2), ._13_2(_13_2),
    ._12_2(_12_2), ._11_2(_11_2), ._10_2(_10_2), ._9_2(_9_2), ._8_2(_8_2), ._7_2(_7_2), ._6_2(_6_2),
    ._5_2(_5_2), ._4_2(_4_2), ._3_2(_3_2), ._2_2(_2_2), ._1_2(_1_2), ._0_2(_0_2), .SUB(alu_f_fun_mux_1_sub),
    .F1(alu_f_fun_mux_1_fa1), .F0(alu_f_fun_mux_1_fa0), .ENA(ENA), .ENB(ENB), .O15(n16_bit_alu_1_o0[15]),
    .out_41(n16_bit_alu_1_o0[14]), .out_42(n16_bit_alu_1_o0[13]), .out_43(n16_bit_alu_1_o0[12]),
    .out_44(n16_bit_alu_1_o0[11]), .out_45(n16_bit_alu_1_o0[10]), .out_46(n16_bit_alu_1_o0[9]),
    .out_47(n16_bit_alu_1_o0[8]), .out_48(n16_bit_alu_1_o0[7]), .out_49(n16_bit_alu_1_o0[6]),
    .out_50(n16_bit_alu_1_o0[5]), .out_51(n16_bit_alu_1_o0[4]), .out_52(n16_bit_alu_1_o0[3]),
    .out_53(n16_bit_alu_1_o0[2]), .out_54(n16_bit_alu_1_o0[1]), .O0(n16_bit_alu_1_o0[0]),
    .OVF(n16_bit_alu_1_ovf[0]), .CARRY(n16_bit_alu_1_carry), .SGN(n16_bit_alu_1_ovf[2]), .INC(1'b0),
    .ZERO(n16_bit_alu_1_ovf[1]));
  LED CARRY (.in(n16_bit_alu_1_carry));
  Multiplexer #(.select(4), .width(16), .enable("false")) multiplexer_1 (
    .in0(alu_nop_block_1_out), .in1(n16_bit_alu_1_o0), .in2(n16_bit_alu_1_o0), .in3(alu_mul_1_output),
    .in4(alu_div_1_div_output), .in5(n16_bit_alu_1_o0), .in6(n16_bit_alu_1_o0), .in7(n16_bit_alu_1_o0),
    .in8(alu_xor_1_out_xor), .out(OUTPUT), .sel({F3, F2, F1, F0}));  // open: in9, in10, in11, in12, in13, in14, in15
  Multiplexer #(.select(4), .width(3), .enable("false")) multiplexer_2 (
    .in0(alu_nop_block_1_ovf), .in1(n16_bit_alu_1_ovf), .in2(n16_bit_alu_1_ovf), .in3(alu_mul_1_ovf),
    .in4(alu_div_1_ovf), .in5(n16_bit_alu_1_ovf), .in6(n16_bit_alu_1_ovf), .in7(n16_bit_alu_1_ovf),
    .in8(alu_xor_1_ovf), .out({SGN, ZERO, OVF}), .sel({F3, F2, F1, F0}));  // open: in9, in10, in11, in12, in13, in14, in15
  ALU_MUL alu_mul_1 (
    .A15(_15), .A14(_14), .A13(_13), .A12(_12), .A11(_11), .A10(_10), .A9(_9), .A8(_8), .A7(_7), .A6(_6),
    .A5(_5), .A4(_4), .A3(_3), .A2(_2), .A1(_1), .A0(_0), .B8(_8_2), .B7(_7_2), .B6(_6_2), .B5(_5_2),
    .B4(_4_2), .B3(_3_2), .B2(_2_2), .B1(_1_2), .B0(_0_2), .B9(_9_2), .B10(_10_2), .B11(_11_2), .B12(_12_2),
    .B13(_13_2), .B14(_14_2), .B15(_15_2), .OUTPUT(alu_mul_1_output), .OVF(alu_mul_1_ovf[0]),
    .ZERO(alu_mul_1_ovf[1]), .SGN(alu_mul_1_ovf[2]));
  ALU_DIV alu_div_1 (
    .ZERO(alu_div_1_ovf[1]), .SGN(alu_div_1_ovf[2]),
    .INPUT_A({_15, _14, _13, _12, _11, _10, _9, _8, _7, _6, _5, _4, _3, _2, _1, _0}),
    .INPUT_B({_15_2, _14_2, _13_2, _12_2, _11_2, _10_2, _9_2, _8_2, _7_2, _6_2, _5_2, _4_2, _3_2, _2_2, _1_2, _0_2}),
    .DIV_OUTPUT(alu_div_1_div_output), .OVF(alu_div_1_ovf[0]), .MOD(alu_div_1_mod));
  ALU_XOR alu_xor_1 (
    .IN_A({_15, _14, _13, _12, _11, _10, _9, _8, _7, _6, _5, _4, _3, _2, _1, _0}),
    .IN_B({_15_2, _14_2, _13_2, _12_2, _11_2, _10_2, _9_2, _8_2, _7_2, _6_2, _5_2, _4_2, _3_2, _2_2, _1_2, _0_2}),
    .SGN(alu_xor_1_ovf[2]), .OVF(alu_xor_1_ovf[0]), .ZERO(alu_xor_1_ovf[1]), .OUT_XOR(alu_xor_1_out_xor));
  Multiplexer #(.select(4), .width(16), .enable("false")) multiplexer_3 (
    .in0({16{1'b0}}), .in1({16{1'b0}}), .in2({16{1'b0}}), .in3({16{1'b0}}), .in4(alu_div_1_mod),
    .in5({16{1'b0}}), .in6({16{1'b0}}), .in7({16{1'b0}}), .in8({16{1'b0}}), .in9({16{1'b0}}),
    .in10({16{1'b0}}), .in11({16{1'b0}}), .in12({16{1'b0}}), .in13({16{1'b0}}), .in14({16{1'b0}}),
    .in15({16{1'b0}}), .out(MOD), .sel({F3, F2, F1, F0}));
  and and_1 (MOD_REG0, ~F0, ~F1, F2, ~F3);  // AND_Gate

  // Notes on the sheet:
  //   A
  //   B
endmodule

// ADD/SUB/NOT/AND/OR
module _16_Bit_ALU (
  input  _15,
  input  _14,
  input  _13,
  input  _12,
  input  _11,
  input  _10,
  input  _9,
  input  _8,
  input  _7,
  input  _6,
  input  _5,
  input  _4,
  input  _3,
  input  _2,
  input  _1,
  input  _0,
  input  _15_2,
  input  _14_2,
  input  _13_2,
  input  _12_2,
  input  _11_2,
  input  _10_2,
  input  _9_2,
  input  _8_2,
  input  _7_2,
  input  _6_2,
  input  _5_2,
  input  _4_2,
  input  _3_2,
  input  _2_2,
  input  _1_2,
  input  _0_2,
  input  SUB,
  input  F1,
  input  F0,
  input  ENA,
  input  ENB,
  input  INC,
  output ZERO,
  output O15,
  output out_41,
  output out_42,
  output out_43,
  output out_44,
  output out_45,
  output out_46,
  output out_47,
  output out_48,
  output out_49,
  output out_50,
  output out_51,
  output out_52,
  output out_53,
  output out_54,
  output O0,
  output OVF,
  output CARRY,
  output SGN
);

  wire and_1_out, and_2_out, and_3_out, and_4_out, and_5_out, and_6_out, and_7_out, and_8_out, and_9_out,
       and_10_out, and_11_out, and_12_out, and_13_out, and_14_out, and_15_out, and_16_out, and_17_out,
       and_18_out, and_19_out, and_20_out, and_21_out, and_22_out, and_23_out, and_24_out, and_25_out,
       and_26_out, and_27_out, and_28_out, and_29_out, and_30_out, and_31_out, and_32_out, and_33_out,
       and_34_out, and_35_out, and_36_out, and_37_out, and_38_out, and_39_out, and_40_out, and_41_out,
       and_42_out, and_43_out, and_44_out, and_45_out, and_46_out, and_47_out, and_48_out, and_49_out,
       and_50_out, and_51_out, and_52_out, and_53_out, and_54_out, and_55_out, and_56_out, and_57_out,
       and_58_out, and_59_out, and_60_out, and_61_out, and_62_out, and_63_out, and_64_out, and_65_out,
       and_66_out, and_67_out, and_68_out, and_69_out, and_70_out, and_71_out, and_72_out, and_73_out,
       and_74_out, and_75_out, and_76_out, and_77_out, and_78_out, and_79_out, and_80_out, and_81_out,
       and_82_out, and_83_out, and_84_out, and_85_out, and_86_out, and_87_out, and_88_out, and_89_out,
       and_90_out, and_91_out, and_92_out, and_93_out, and_94_out, and_95_out, and_96_out, and_97_out,
       and_98_out, and_99_out, and_100_out, and_101_out, and_102_out, and_103_out, and_104_out, and_105_out,
       and_106_out, and_107_out, and_108_out, and_109_out, and_110_out, and_111_out, and_112_out,
       and_113_out, and_114_out, and_115_out, and_116_out, and_117_out, and_118_out, and_119_out,
       and_120_out, and_121_out, and_122_out, and_123_out, and_124_out, and_125_out, and_126_out,
       and_127_out, and_128_out, and_129_out, and_130_out, and_131_out, and_132_out, and_133_out,
       and_134_out, and_135_out, and_136_out, and_137_out, and_138_out, and_139_out, and_140_out,
       and_141_out, and_142_out, and_143_out, and_144_out, and_145_out, and_146_out, and_147_out,
       and_148_out, and_149_out, and_150_out, and_151_out, and_152_out, and_153_out, and_154_out,
       and_155_out, and_156_out, and_157_out, and_158_out, and_159_out, and_160_out, and_161_out,
       and_162_out, and_163_out, and_164_out, and_165_out, and_166_out, and_167_out, and_168_out,
       and_169_out, and_170_out, and_171_out, and_172_out, and_173_out, and_174_out, and_175_out,
       and_176_out, and_177_out, and_178_out, and_179_out, and_180_out, and_181_out, and_182_out,
       and_183_out, and_184_out, and_185_out, and_186_out, and_187_out, and_188_out, and_189_out,
       and_190_out, and_191_out, and_192_out, and_193_out, and_194_out, and_195_out, and_196_out,
       and_197_out, and_198_out, and_199_out, and_200_out, and_201_out, and_202_out, and_203_out,
       and_204_out, and_205_out, and_206_out, and_207_out, and_208_out, and_209_out, and_210_out,
       and_211_out, and_212_out, and_213_out, and_214_out, and_215_out, and_216_out, and_217_out,
       and_218_out, and_219_out, and_220_out, and_221_out, and_222_out, and_223_out, and_224_out,
       and_225_out, and_226_out, and_227_out, and_228_out, and_229_out, and_230_out, and_231_out,
       and_232_out, and_233_out, and_234_out, and_235_out, and_236_out, and_237_out, and_238_out,
       and_239_out, and_240_out, not_1_out, not_2_out, not_3_out, not_4_out, not_5_out, not_6_out, not_7_out,
       not_8_out, not_9_out, not_10_out, not_11_out, not_12_out, not_13_out, not_14_out, not_15_out,
       not_16_out, not_17_out, not_18_out, not_19_out, not_20_out, not_21_out, not_22_out, not_23_out,
       not_24_out, not_25_out, not_26_out, not_27_out, not_28_out, not_29_out, not_30_out, not_31_out,
       not_32_out, not_33_out, not_34_out, not_35_out, not_36_out, not_37_out, not_38_out, not_39_out,
       not_40_out, not_41_out, not_42_out, not_43_out, not_44_out, not_45_out, not_46_out, not_47_out,
       not_48_out, not_49_out, not_50_out, not_51_out, not_52_out, not_53_out, not_55_out, not_56_out,
       not_57_out, not_58_out, not_59_out, not_60_out, not_61_out, not_62_out, not_63_out, not_64_out,
       not_65_out, not_66_out, not_67_out, not_68_out, not_69_out, not_70_out, not_71_out, not_72_out,
       not_73_out, not_74_out, not_75_out, not_76_out, not_77_out, not_78_out, not_79_out, not_80_out,
       not_81_out, not_82_out, not_83_out, not_84_out, not_85_out, not_86_out, not_87_out, not_88_out,
       not_89_out, not_90_out, not_91_out, not_92_out, not_93_out, not_94_out, not_95_out, not_96_out,
       not_97_out, not_98_out, not_99_out, not_100_out, not_101_out, not_102_out, not_103_out, not_104_out,
       not_105_out, not_106_out, not_107_out, not_108_out, not_109_out, not_110_out, not_111_out,
       not_112_out, not_113_out, not_114_out, or_1_out, or_2_out, or_3_out, or_4_out, or_5_out, or_6_out,
       or_7_out, or_8_out, or_9_out, or_10_out, or_11_out, or_12_out, or_13_out, or_14_out, or_15_out,
       or_16_out, or_17_out, or_18_out, or_19_out, or_20_out, or_21_out, or_22_out, or_23_out, or_24_out,
       or_25_out, or_26_out, or_27_out, or_28_out, or_33_out, or_34_out, or_35_out, or_36_out, or_37_out,
       or_38_out, or_39_out, or_40_out, or_45_out, or_46_out, or_47_out, or_48_out, or_49_out, or_50_out,
       or_51_out, or_52_out, or_57_out, or_58_out, or_59_out, or_60_out, or_61_out, or_62_out, or_63_out,
       or_64_out, xor_1_out, xor_2_out, xor_3_out, xor_4_out, xor_5_out, xor_6_out, xor_7_out, xor_8_out,
       xor_9_out, xor_10_out, xor_11_out, xor_12_out, xor_13_out, xor_14_out, xor_15_out, xor_16_out,
       xor_17_out, xor_18_out, xor_19_out, xor_20_out, xor_21_out, xor_22_out, xor_23_out, xor_24_out,
       xor_25_out, xor_26_out, xor_27_out, xor_28_out, xor_30_out, xor_31_out, xor_32_out, xor_33_out;

  not not_1 (not_1_out, SUB);
  and and_1 (and_1_out, not_1_out, _15_2);
  or or_1 (or_1_out, and_1_out, and_5_out);
  not not_2 (not_2_out, SUB);
  and and_2 (and_2_out, not_2_out, _13_2);
  or or_2 (or_2_out, and_2_out, and_8_out);
  not not_3 (not_3_out, SUB);
  and and_3 (and_3_out, not_3_out, _11_2);
  or or_3 (or_3_out, and_3_out, and_9_out);
  not not_4 (not_4_out, SUB);
  and and_4 (and_4_out, not_4_out, _9_2);
  or or_4 (or_4_out, and_4_out, and_11_out);
  not not_5 (not_5_out, _15_2);
  not not_6 (not_6_out, _14_2);
  not not_7 (not_7_out, SUB);
  and and_5 (and_5_out, not_5_out, SUB);
  and and_6 (and_6_out, not_7_out, _14_2);
  or or_5 (or_5_out, and_6_out, and_13_out);
  not not_8 (not_8_out, _13_2);
  not not_9 (not_9_out, _12_2);
  not not_10 (not_10_out, SUB);
  and and_7 (and_7_out, not_10_out, _12_2);
  and and_8 (and_8_out, not_8_out, SUB);
  or or_6 (or_6_out, and_7_out, and_14_out);
  not not_11 (not_11_out, _10_2);
  not not_12 (not_12_out, _11_2);
  not not_13 (not_13_out, SUB);
  and and_9 (and_9_out, not_12_out, SUB);
  and and_10 (and_10_out, not_13_out, _10_2);
  or or_7 (or_7_out, and_10_out, and_15_out);
  not not_14 (not_14_out, _9_2);
  not not_15 (not_15_out, _8_2);
  not not_16 (not_16_out, SUB);
  and and_11 (and_11_out, not_14_out, SUB);
  and and_12 (and_12_out, not_16_out, _8_2);
  or or_8 (or_8_out, and_12_out, and_16_out);
  and and_13 (and_13_out, not_6_out, SUB);
  and and_14 (and_14_out, not_9_out, SUB);
  and and_15 (and_15_out, not_11_out, SUB);
  and and_16 (and_16_out, not_15_out, SUB);
  not not_17 (not_17_out, _1_2);
  not not_18 (not_18_out, SUB);
  and and_17 (and_17_out, not_18_out, _1_2);
  or or_9 (or_9_out, and_17_out, and_21_out);
  not not_19 (not_19_out, _3_2);
  not not_20 (not_20_out, SUB);
  and and_18 (and_18_out, not_20_out, _3_2);
  or or_10 (or_10_out, and_18_out, and_26_out);
  not not_21 (not_21_out, _5_2);
  not not_22 (not_22_out, SUB);
  and and_19 (and_19_out, not_22_out, _5_2);
  or or_11 (or_11_out, and_19_out, and_29_out);
  not not_23 (not_23_out, _7_2);
  not not_24 (not_24_out, SUB);
  and and_20 (and_20_out, not_24_out, _7_2);
  or or_12 (or_12_out, and_20_out, and_31_out);
  not not_25 (not_25_out, _0_2);
  not not_26 (not_26_out, SUB);
  and and_21 (and_21_out, not_17_out, SUB);
  and and_22 (and_22_out, not_26_out, _0_2);
  and and_23 (and_23_out, not_25_out, SUB);
  or or_13 (or_13_out, and_22_out, and_23_out);
  not not_27 (not_27_out, _2_2);
  not not_28 (not_28_out, SUB);
  and and_24 (and_24_out, not_27_out, SUB);
  and and_25 (and_25_out, not_28_out, _2_2);
  and and_26 (and_26_out, not_19_out, SUB);
  or or_14 (or_14_out, and_25_out, and_24_out);
  not not_29 (not_29_out, _4_2);
  not not_30 (not_30_out, SUB);
  and and_27 (and_27_out, not_30_out, _4_2);
  and and_28 (and_28_out, not_29_out, SUB);
  and and_29 (and_29_out, not_21_out, SUB);
  or or_15 (or_15_out, and_27_out, and_28_out);
  not not_31 (not_31_out, _6_2);
  not not_32 (not_32_out, SUB);
  and and_30 (and_30_out, not_32_out, _6_2);
  and and_31 (and_31_out, not_23_out, SUB);
  and and_32 (and_32_out, not_31_out, SUB);
  or or_16 (or_16_out, and_30_out, and_32_out);
  or or_17 (or_17_out, F0, SUB);
  or or_18 (or_18_out, F1, SUB);
  LED u_Carry (.in(CARRY));
  LED u_OVF (.in(OVF));
  Multiplexer #(.enable("false")) multiplexer_1 (.in0(or_62_out), .in1(not_33_out), .out(CARRY), .sel(SUB));
  and and_33 (and_33_out, ENA, _0);
  and and_34 (and_34_out, ENB, or_13_out);
  and and_35 (and_35_out, ENA, _1);
  and and_36 (and_36_out, ENB, or_9_out);
  and and_37 (and_37_out, ENA, _4);
  and and_38 (and_38_out, ENB, or_15_out);
  and and_39 (and_39_out, ENA, _5);
  and and_40 (and_40_out, ENB, or_11_out);
  LED led_1 (.in(O15));
  LED led_2 (.in(out_41));
  not not_33 (not_33_out, or_62_out);
  or or_19 (or_19_out, SUB, INC);
  and and_41 (and_41_out, and_33_out, and_34_out);
  or or_20 (or_20_out, and_33_out, and_34_out);
  not not_34 (not_34_out, and_34_out);
  not not_35 (not_35_out, or_17_out);
  and and_42 (and_42_out, not_35_out, not_36_out);
  not not_36 (not_36_out, or_18_out);
  and and_43 (and_43_out, or_17_out, not_37_out);
  not not_37 (not_37_out, or_18_out);
  not not_38 (not_38_out, or_17_out);
  and and_44 (and_44_out, not_38_out, or_18_out);
  and and_45 (and_45_out, or_17_out, or_18_out);
  and and_46 (and_46_out, and_35_out, and_36_out);
  or or_21 (or_21_out, and_35_out, and_36_out);
  not not_39 (not_39_out, and_36_out);
  not not_40 (not_40_out, or_17_out);
  and and_47 (and_47_out, not_40_out, not_41_out);
  not not_41 (not_41_out, or_18_out);
  and and_48 (and_48_out, or_17_out, not_42_out);
  not not_42 (not_42_out, or_18_out);
  not not_43 (not_43_out, or_17_out);
  and and_49 (and_49_out, not_43_out, or_18_out);
  and and_50 (and_50_out, or_17_out, or_18_out);
  and and_51 (and_51_out, and_37_out, and_38_out);
  or or_22 (or_22_out, and_37_out, and_38_out);
  not not_44 (not_44_out, and_38_out);
  not not_45 (not_45_out, or_17_out);
  and and_52 (and_52_out, not_45_out, not_46_out);
  not not_46 (not_46_out, or_18_out);
  and and_53 (and_53_out, or_17_out, not_47_out);
  not not_47 (not_47_out, or_18_out);
  not not_48 (not_48_out, or_17_out);
  and and_54 (and_54_out, not_48_out, or_18_out);
  and and_55 (and_55_out, or_17_out, or_18_out);
  and and_56 (and_56_out, and_39_out, and_40_out);
  or or_23 (or_23_out, and_39_out, and_40_out);
  not not_49 (not_49_out, and_40_out);
  not not_50 (not_50_out, or_17_out);
  and and_57 (and_57_out, not_50_out, not_51_out);
  not not_51 (not_51_out, or_18_out);
  and and_58 (and_58_out, or_17_out, not_52_out);
  not not_52 (not_52_out, or_18_out);
  not not_53 (not_53_out, or_17_out);
  and and_59 (and_59_out, not_53_out, or_18_out);
  and and_60 (and_60_out, or_17_out, or_18_out);
  LED led_3 (.in(out_44));
  LED led_4 (.in(out_42));
  LED led_5 (.in(out_43));
  LED led_6 (.in(out_45));
  LED led_7 (.in(out_47));
  LED led_8 (.in(out_46));
  LED led_9 (.in(out_48));
  and and_61 (and_61_out, and_34_out, and_45_out, and_33_out);
  and and_62 (and_62_out, and_36_out, and_50_out, and_35_out);
  and and_63 (and_63_out, and_38_out, and_55_out, and_37_out);
  and and_64 (and_64_out, and_40_out, and_60_out, and_39_out);
  LED led_10 (.in(out_51));
  LED led_11 (.in(out_50));
  LED led_12 (.in(out_49));
  and and_65 (and_65_out, and_41_out, and_43_out);
  and and_66 (and_66_out, or_20_out, and_42_out);
  and and_67 (and_67_out, not_34_out, and_44_out);
  xor xor_1 (xor_1_out, and_33_out, and_34_out);
  and and_68 (and_68_out, xor_1_out, and_45_out, or_19_out);
  or or_24 (or_24_out, and_61_out, and_68_out);
  and and_69 (and_69_out, and_46_out, and_48_out);
  and and_70 (and_70_out, or_21_out, and_47_out);
  and and_71 (and_71_out, not_39_out, and_49_out);
  xor xor_2 (xor_2_out, and_35_out, and_36_out);
  and and_72 (and_72_out, xor_2_out, and_50_out, or_24_out);
  or or_25 (or_25_out, and_62_out, and_72_out);
  and and_73 (and_73_out, and_51_out, and_53_out);
  and and_74 (and_74_out, or_22_out, and_52_out);
  and and_75 (and_75_out, not_44_out, and_54_out);
  xor xor_3 (xor_3_out, and_37_out, and_38_out);
  and and_76 (and_76_out, xor_3_out, and_55_out, or_37_out);
  or or_26 (or_26_out, and_63_out, and_76_out);
  and and_77 (and_77_out, and_56_out, and_58_out);
  and and_78 (and_78_out, or_23_out, and_57_out);
  and and_79 (and_79_out, not_49_out, and_59_out);
  xor xor_4 (xor_4_out, and_39_out, and_40_out);
  and and_80 (and_80_out, xor_4_out, and_60_out, or_26_out);
  or or_27 (or_27_out, and_64_out, and_80_out);
  LED led_13 (.in(out_53));
  LED led_14 (.in(O0));
  LED led_15 (.in(out_52));
  LED led_16 (.in(out_54));
  xor xor_5 (xor_5_out, or_19_out, xor_1_out);
  xor xor_6 (xor_6_out, or_24_out, xor_2_out);
  xor xor_7 (xor_7_out, or_37_out, xor_3_out);
  xor xor_8 (xor_8_out, or_26_out, xor_4_out);
  and and_81 (and_81_out, xor_5_out, and_45_out);
  and and_82 (and_82_out, xor_6_out, and_50_out);
  and and_83 (and_83_out, xor_7_out, and_55_out);
  and and_84 (and_84_out, xor_8_out, and_60_out);
  not not_54 (ZERO, or_28_out);
  or or_28 (or_28_out, out_48, out_49, out_50, out_51, out_52, out_53, out_54, O0, out_47, out_46, out_45, out_44, out_43, out_42, out_41, O15);
  or or_29 (O0, and_65_out, and_66_out, and_67_out, and_81_out);
  or or_30 (out_54, and_69_out, and_70_out, and_71_out, and_82_out);
  or or_31 (out_51, and_73_out, and_74_out, and_75_out, and_83_out);
  or or_32 (out_50, and_77_out, and_78_out, and_79_out, and_84_out);
  not not_55 (not_55_out, or_17_out);
  and and_85 (and_85_out, not_55_out, not_56_out);
  not not_56 (not_56_out, or_18_out);
  and and_86 (and_86_out, or_17_out, not_57_out);
  not not_57 (not_57_out, or_18_out);
  not not_58 (not_58_out, or_17_out);
  and and_87 (and_87_out, not_58_out, or_18_out);
  and and_88 (and_88_out, or_17_out, or_18_out);
  and and_89 (and_89_out, ENA, _3);
  and and_90 (and_90_out, ENB, or_10_out);
  not not_59 (not_59_out, or_17_out);
  and and_91 (and_91_out, not_59_out, not_60_out);
  not not_60 (not_60_out, or_18_out);
  and and_92 (and_92_out, or_17_out, not_61_out);
  not not_61 (not_61_out, or_18_out);
  not not_62 (not_62_out, or_17_out);
  and and_93 (and_93_out, not_62_out, or_18_out);
  and and_94 (and_94_out, or_17_out, or_18_out);
  and and_95 (and_95_out, ENA, _2);
  and and_96 (and_96_out, ENB, or_14_out);
  not not_63 (not_63_out, or_17_out);
  and and_97 (and_97_out, not_63_out, not_64_out);
  not not_64 (not_64_out, or_18_out);
  and and_98 (and_98_out, or_17_out, not_65_out);
  not not_65 (not_65_out, or_18_out);
  not not_66 (not_66_out, or_17_out);
  and and_99 (and_99_out, not_66_out, or_18_out);
  and and_100 (and_100_out, or_17_out, or_18_out);
  and and_101 (and_101_out, ENA, _7);
  and and_102 (and_102_out, ENB, or_12_out);
  not not_67 (not_67_out, or_17_out);
  and and_103 (and_103_out, not_67_out, not_68_out);
  not not_68 (not_68_out, or_18_out);
  and and_104 (and_104_out, or_17_out, not_69_out);
  not not_69 (not_69_out, or_18_out);
  not not_70 (not_70_out, or_17_out);
  and and_105 (and_105_out, not_70_out, or_18_out);
  and and_106 (and_106_out, or_17_out, or_18_out);
  and and_107 (and_107_out, ENA, _6);
  and and_108 (and_108_out, ENB, or_16_out);
  and and_109 (and_109_out, and_89_out, and_90_out);
  or or_33 (or_33_out, and_89_out, and_90_out);
  not not_71 (not_71_out, and_90_out);
  and and_110 (and_110_out, and_95_out, and_96_out);
  or or_34 (or_34_out, and_95_out, and_96_out);
  not not_72 (not_72_out, and_96_out);
  and and_111 (and_111_out, and_101_out, and_102_out);
  or or_35 (or_35_out, and_101_out, and_102_out);
  not not_73 (not_73_out, and_102_out);
  and and_112 (and_112_out, and_107_out, and_108_out);
  or or_36 (or_36_out, and_107_out, and_108_out);
  not not_74 (not_74_out, and_108_out);
  and and_113 (and_113_out, and_89_out, and_88_out, and_90_out);
  and and_114 (and_114_out, and_109_out, and_86_out);
  and and_115 (and_115_out, or_33_out, and_85_out);
  and and_116 (and_116_out, not_71_out, and_87_out);
  and and_117 (and_117_out, and_95_out, and_94_out, and_96_out);
  and and_118 (and_118_out, and_110_out, and_92_out);
  and and_119 (and_119_out, or_34_out, and_91_out);
  and and_120 (and_120_out, not_72_out, and_93_out);
  and and_121 (and_121_out, and_101_out, and_100_out, and_102_out);
  and and_122 (and_122_out, and_111_out, and_98_out);
  and and_123 (and_123_out, or_35_out, and_97_out);
  and and_124 (and_124_out, not_73_out, and_99_out);
  and and_125 (and_125_out, and_107_out, and_106_out, and_108_out);
  and and_126 (and_126_out, and_112_out, and_104_out);
  and and_127 (and_127_out, or_36_out, and_103_out);
  and and_128 (and_128_out, not_74_out, and_105_out);
  or or_37 (or_37_out, and_113_out, and_129_out);
  and and_129 (and_129_out, xor_9_out, and_88_out, or_38_out);
  xor xor_9 (xor_9_out, and_89_out, and_90_out);
  or or_38 (or_38_out, and_117_out, and_130_out);
  and and_130 (and_130_out, xor_10_out, and_94_out, or_25_out);
  xor xor_10 (xor_10_out, and_95_out, and_96_out);
  or or_39 (or_39_out, and_121_out, and_131_out);
  and and_131 (and_131_out, xor_11_out, and_100_out, or_40_out);
  xor xor_11 (xor_11_out, and_101_out, and_102_out);
  or or_40 (or_40_out, and_125_out, and_132_out);
  and and_132 (and_132_out, xor_12_out, and_106_out, or_27_out);
  xor xor_12 (xor_12_out, and_107_out, and_108_out);
  xor xor_13 (xor_13_out, xor_9_out, or_38_out);
  xor xor_14 (xor_14_out, xor_10_out, or_25_out);
  xor xor_15 (xor_15_out, xor_11_out, or_40_out);
  xor xor_16 (xor_16_out, xor_12_out, or_27_out);
  and and_133 (and_133_out, and_88_out, xor_13_out);
  and and_134 (and_134_out, and_94_out, xor_14_out);
  and and_135 (and_135_out, and_100_out, xor_15_out);
  and and_136 (and_136_out, and_106_out, xor_16_out);
  or or_41 (out_52, and_133_out, and_114_out, and_115_out, and_116_out);
  or or_42 (out_53, and_134_out, and_118_out, and_119_out, and_120_out);
  or or_43 (out_48, and_135_out, and_122_out, and_123_out, and_124_out);
  or or_44 (out_49, and_136_out, and_126_out, and_127_out, and_128_out);
  and and_137 (and_137_out, ENA, _8);
  and and_138 (and_138_out, ENB, or_8_out);
  not not_75 (not_75_out, or_17_out);
  not not_76 (not_76_out, or_18_out);
  not not_77 (not_77_out, or_18_out);
  not not_78 (not_78_out, or_17_out);
  and and_139 (and_139_out, ENA, _9);
  and and_140 (and_140_out, ENB, or_4_out);
  not not_79 (not_79_out, or_17_out);
  not not_80 (not_80_out, or_18_out);
  not not_81 (not_81_out, or_18_out);
  not not_82 (not_82_out, or_17_out);
  not not_83 (not_83_out, or_17_out);
  and and_141 (and_141_out, not_83_out, not_84_out);
  not not_84 (not_84_out, or_18_out);
  and and_142 (and_142_out, or_17_out, not_85_out);
  not not_85 (not_85_out, or_18_out);
  not not_86 (not_86_out, or_17_out);
  and and_143 (and_143_out, not_86_out, or_18_out);
  and and_144 (and_144_out, or_17_out, or_18_out);
  and and_145 (and_145_out, ENA, _13);
  and and_146 (and_146_out, ENB, or_2_out);
  not not_87 (not_87_out, or_17_out);
  and and_147 (and_147_out, not_87_out, not_88_out);
  not not_88 (not_88_out, or_18_out);
  and and_148 (and_148_out, or_17_out, not_89_out);
  not not_89 (not_89_out, or_18_out);
  not not_90 (not_90_out, or_17_out);
  and and_149 (and_149_out, not_90_out, or_18_out);
  and and_150 (and_150_out, or_17_out, or_18_out);
  and and_151 (and_151_out, ENA, _12);
  and and_152 (and_152_out, ENB, or_6_out);
  and and_153 (and_153_out, and_137_out, and_138_out);
  or or_45 (or_45_out, and_137_out, and_138_out);
  not not_91 (not_91_out, and_138_out);
  and and_154 (and_154_out, not_75_out, not_76_out);
  and and_155 (and_155_out, or_17_out, not_77_out);
  and and_156 (and_156_out, not_78_out, or_18_out);
  and and_157 (and_157_out, or_17_out, or_18_out);
  and and_158 (and_158_out, and_139_out, and_140_out);
  or or_46 (or_46_out, and_139_out, and_140_out);
  not not_92 (not_92_out, and_140_out);
  and and_159 (and_159_out, not_79_out, not_80_out);
  and and_160 (and_160_out, or_17_out, not_81_out);
  and and_161 (and_161_out, not_82_out, or_18_out);
  and and_162 (and_162_out, or_17_out, or_18_out);
  and and_163 (and_163_out, and_145_out, and_146_out);
  or or_47 (or_47_out, and_145_out, and_146_out);
  not not_93 (not_93_out, and_146_out);
  and and_164 (and_164_out, and_151_out, and_152_out);
  or or_48 (or_48_out, and_151_out, and_152_out);
  not not_94 (not_94_out, and_152_out);
  and and_165 (and_165_out, and_153_out, and_155_out);
  and and_166 (and_166_out, or_45_out, and_154_out);
  and and_167 (and_167_out, not_91_out, and_156_out);
  and and_168 (and_168_out, and_138_out, and_157_out, and_137_out);
  or or_49 (or_49_out, and_168_out, and_181_out);
  and and_169 (and_169_out, and_158_out, and_160_out);
  and and_170 (and_170_out, or_46_out, and_159_out);
  and and_171 (and_171_out, not_92_out, and_161_out);
  and and_172 (and_172_out, and_140_out, and_162_out, and_139_out);
  or or_50 (or_50_out, and_172_out, and_182_out);
  and and_173 (and_173_out, and_145_out, and_144_out, and_146_out);
  and and_174 (and_174_out, and_163_out, and_142_out);
  and and_175 (and_175_out, or_47_out, and_141_out);
  and and_176 (and_176_out, not_93_out, and_143_out);
  and and_177 (and_177_out, and_151_out, and_150_out, and_152_out);
  and and_178 (and_178_out, and_164_out, and_148_out);
  and and_179 (and_179_out, or_48_out, and_147_out);
  and and_180 (and_180_out, not_94_out, and_149_out);
  xor xor_17 (xor_17_out, and_137_out, and_138_out);
  and and_181 (and_181_out, xor_17_out, and_157_out, or_39_out);
  xor xor_18 (xor_18_out, and_139_out, and_140_out);
  and and_182 (and_182_out, xor_18_out, and_162_out, or_49_out);
  or or_51 (or_51_out, and_173_out, and_183_out);
  and and_183 (and_183_out, xor_19_out, and_144_out, or_52_out);
  xor xor_19 (xor_19_out, and_145_out, and_146_out);
  or or_52 (or_52_out, and_177_out, and_184_out);
  and and_184 (and_184_out, xor_20_out, and_150_out, or_63_out);
  xor xor_20 (xor_20_out, and_151_out, and_152_out);
  xor xor_21 (xor_21_out, or_39_out, xor_17_out);
  and and_185 (and_185_out, xor_21_out, and_157_out);
  xor xor_22 (xor_22_out, or_49_out, xor_18_out);
  and and_186 (and_186_out, xor_22_out, and_162_out);
  xor xor_23 (xor_23_out, xor_19_out, or_52_out);
  xor xor_24 (xor_24_out, xor_20_out, or_63_out);
  or or_53 (out_47, and_165_out, and_166_out, and_167_out, and_185_out);
  or or_54 (out_46, and_169_out, and_170_out, and_171_out, and_186_out);
  and and_187 (and_187_out, and_144_out, xor_23_out);
  and and_188 (and_188_out, and_150_out, xor_24_out);
  or or_55 (out_42, and_187_out, and_174_out, and_175_out, and_176_out);
  or or_56 (out_43, and_188_out, and_178_out, and_179_out, and_180_out);
  not not_95 (not_95_out, or_17_out);
  and and_189 (and_189_out, not_95_out, not_96_out);
  not not_96 (not_96_out, or_18_out);
  and and_190 (and_190_out, or_17_out, not_97_out);
  not not_97 (not_97_out, or_18_out);
  not not_98 (not_98_out, or_17_out);
  and and_191 (and_191_out, not_98_out, or_18_out);
  and and_192 (and_192_out, or_17_out, or_18_out);
  and and_193 (and_193_out, ENA, _11);
  and and_194 (and_194_out, ENB, or_3_out);
  not not_99 (not_99_out, or_17_out);
  and and_195 (and_195_out, not_99_out, not_100_out);
  not not_100 (not_100_out, or_18_out);
  and and_196 (and_196_out, or_17_out, not_101_out);
  not not_101 (not_101_out, or_18_out);
  not not_102 (not_102_out, or_17_out);
  and and_197 (and_197_out, not_102_out, or_18_out);
  and and_198 (and_198_out, or_17_out, or_18_out);
  and and_199 (and_199_out, ENA, _10);
  and and_200 (and_200_out, ENB, or_7_out);
  and and_201 (and_201_out, ENA, _14);
  and and_202 (and_202_out, ENB, or_5_out);
  not not_103 (not_103_out, or_17_out);
  not not_104 (not_104_out, or_18_out);
  not not_105 (not_105_out, or_18_out);
  not not_106 (not_106_out, or_17_out);
  and and_203 (and_203_out, ENA, _15);
  and and_204 (and_204_out, ENB, or_1_out);
  not not_107 (not_107_out, or_17_out);
  not not_108 (not_108_out, or_18_out);
  not not_109 (not_109_out, or_18_out);
  not not_110 (not_110_out, or_17_out);
  and and_205 (and_205_out, and_193_out, and_194_out);
  or or_57 (or_57_out, and_193_out, and_194_out);
  not not_111 (not_111_out, and_194_out);
  and and_206 (and_206_out, and_199_out, and_200_out);
  or or_58 (or_58_out, and_199_out, and_200_out);
  not not_112 (not_112_out, and_200_out);
  and and_207 (and_207_out, and_201_out, and_202_out);
  or or_59 (or_59_out, and_201_out, and_202_out);
  not not_113 (not_113_out, and_202_out);
  and and_208 (and_208_out, not_103_out, not_104_out);
  and and_209 (and_209_out, or_17_out, not_105_out);
  and and_210 (and_210_out, not_106_out, or_18_out);
  and and_211 (and_211_out, or_17_out, or_18_out);
  and and_212 (and_212_out, and_203_out, and_204_out);
  or or_60 (or_60_out, and_203_out, and_204_out);
  not not_114 (not_114_out, and_204_out);
  and and_213 (and_213_out, not_107_out, not_108_out);
  and and_214 (and_214_out, or_17_out, not_109_out);
  and and_215 (and_215_out, not_110_out, or_18_out);
  and and_216 (and_216_out, or_17_out, or_18_out);
  and and_217 (and_217_out, and_205_out, and_190_out);
  and and_218 (and_218_out, or_57_out, and_189_out);
  and and_219 (and_219_out, not_111_out, and_191_out);
  and and_220 (and_220_out, and_206_out, and_196_out);
  and and_221 (and_221_out, or_58_out, and_195_out);
  and and_222 (and_222_out, not_112_out, and_197_out);
  and and_223 (and_223_out, and_207_out, and_209_out);
  and and_224 (and_224_out, or_59_out, and_208_out);
  and and_225 (and_225_out, not_113_out, and_210_out);
  and and_226 (and_226_out, and_202_out, and_211_out, and_201_out);
  or or_61 (or_61_out, and_226_out, and_233_out);
  and and_227 (and_227_out, and_212_out, and_214_out);
  and and_228 (and_228_out, or_60_out, and_213_out);
  and and_229 (and_229_out, not_114_out, and_215_out);
  and and_230 (and_230_out, and_204_out, and_216_out, and_203_out);
  or or_62 (or_62_out, and_230_out, and_234_out);
  or or_63 (or_63_out, and_231_out, and_235_out);
  and and_231 (and_231_out, and_193_out, and_192_out, and_194_out);
  or or_64 (or_64_out, and_232_out, and_236_out);
  and and_232 (and_232_out, and_199_out, and_198_out, and_200_out);
  xor xor_25 (xor_25_out, and_201_out, and_202_out);
  and and_233 (and_233_out, xor_25_out, and_211_out, or_51_out);
  xor xor_26 (xor_26_out, and_203_out, and_204_out);
  and and_234 (and_234_out, xor_26_out, and_216_out, or_61_out);
  and and_235 (and_235_out, xor_27_out, and_192_out, or_64_out);
  xor xor_27 (xor_27_out, and_193_out, and_194_out);
  and and_236 (and_236_out, xor_28_out, and_198_out, or_50_out);
  xor xor_28 (xor_28_out, and_199_out, and_200_out);
  xor xor_29 (OVF, or_51_out, or_62_out);
  xor xor_30 (xor_30_out, or_51_out, xor_25_out);
  and and_237 (and_237_out, xor_30_out, and_211_out);
  xor xor_31 (xor_31_out, or_61_out, xor_26_out);
  and and_238 (and_238_out, xor_31_out, and_216_out);
  and and_239 (and_239_out, and_192_out, xor_32_out);
  xor xor_32 (xor_32_out, xor_27_out, or_64_out);
  and and_240 (and_240_out, and_198_out, xor_33_out);
  xor xor_33 (xor_33_out, xor_28_out, or_50_out);
  or or_65 (out_41, and_223_out, and_224_out, and_225_out, and_237_out);
  or or_66 (O15, and_227_out, and_228_out, and_229_out, and_238_out);
  or or_67 (out_44, and_239_out, and_217_out, and_218_out, and_219_out);
  or or_68 (out_45, and_240_out, and_220_out, and_221_out, and_222_out);

  assign SGN = O15;

  // Notes on the sheet:
  //   A
  //   INPUT
  //   B
  //   16-Bit ALU
  //   OR / AND / NOT
  //   INC / ADD / SUB
  //   Made by Hamudi
  //   CU
  //   F0
  //   F1
  //   F0
  //   F1
  //   F0
  //   F1
  //   F0
  //   F1
  //   A * B
  //   A + B
  //   -B
  //   00: A + B
  //   01: A*B
  //   10: -B
  //   11: A + B (ALU)
  //   A * B
  //   A + B
  //   -B
  //   00: A + B
  //   01: A*B
  //   10: -B
  //   11: A + B (ALU)
  //   A * B
  //   A + B
  //   -B
  //   00: A + B
  //   01: A*B
  //   10: -B
  //   11: A + B (ALU)
  //   A * B
  //   A + B
  //   -B
  //   00: A + B
  //   01: A*B
  //   10: -B
  //   11: A + B (ALU)
  //   OUTPUT
  //   Carry-Out 0
  //   Carry-Out 1
  //   Carry-Out 4
  //   Carry-Out 5
  //   CI0
  //   CI1
  //   CI4
  //   CI5
  //   B0
  //   B1
  //   B4
  //   B5
  //   F0
  //   F1
  //   F0
  //   F1
  //   F0
  //   F1
  //   F0
  //   F1
  //   00: A + B
  //   01: A*B
  //   10: -B
  //   00: A + B
  //   01: A*B
  //   10: -B
  //   00: A + B
  //   01: A*B
  //   10: -B
  //   00: A + B
  //   01: A*B
  //   10: -B
  //   11: A + B (ALU)
  //   A * B
  //   A + B
  //   -B
  //   11: A + B (ALU)
  //   A * B
  //   A + B
  //   -B
  //   11: A + B (ALU)
  //   A * B
  //   A + B
  //   -B
  //   11: A + B (ALU)
  //   A * B
  //   A + B
  //   -B
  //   Carry-Out 3
  //   Carry-Out 7
  //   Carry-Out 2
  //   Carry-In 2
  //   Carry-Out 6
  //   Carry-In 6
  //   CI3
  //   CI7
  //   B4
  //   B3
  //   B7
  //   B6
  //   F0
  //   F1
  //   F0
  //   F1
  //   F0
  //   F1
  //   F0
  //   F1
  //   00: A + B
  //   01: A*B
  //   10: -B
  //   00: A + B
  //   01: A*B
  //   10: -B
  //   A * B
  //   A + B
  //   -B
  //   00: A + B
  //   01: A*B
  //   10: -B
  //   11: A + B (ALU)
  //   A * B
  //   A + B
  //   -B
  //   00: A + B
  //   01: A*B
  //   10: -B
  //   11: A + B (ALU)
  //   11: A + B (ALU)
  //   A * B
  //   A + B
  //   -B
  //   11: A + B (ALU)
  //   A * B
  //   A + B
  //   -B
  //   CI8
  //   Carry-Out 8
  //   CI9
  //   Carry-Out 9
  //   Carry-Out 13
  //   Carry-Out 12
  //   Carry-In 12
  //   CI13
  //   B8
  //   B9
  //   B13
  //   B12
  //   F0
  //   F1
  //   F0
  //   F1
  //   F0
  //   F1
  //   F0
  //   F1
  //   00: A + B
  //   01: A*B
  //   10: -B
  //   11: A + B (ALU)
  //   00: A + B
  //   01: A*B
  //   10: -B
  //   11: A + B (ALU)
  //   A * B
  //   A + B
  //   -B
  //   00: A + B
  //   01: A*B
  //   10: -B
  //   11: A + B (ALU)
  //   A * B
  //   A + B
  //   -B
  //   00: A + B
  //   01: A*B
  //   10: -B
  //   11: A + B (ALU)
  //   A * B
  //   A + B
  //   -B
  //   A * B
  //   A + B
  //   -B
  //   Carry-In 14
  //   Carry-Out 11
  //   Carry-In 10
  //   Carry-Out 14
  //   CI15
  //   Carry-Out 15 (OVF)
  //   CI11
  //   Carry-Out 10
  //   B14
  //   B15
  //   B11
  //   B10
endmodule

// NOP/CMP
module ALU_NOP_BLOCK (
  input  [15:0] IN_A,
  input  [15:0] IN_B,
  input  ENA,
  input  ENB,
  output SGN,
  output [15:0] OUT,
  output ZERO,
  output OVF
);

  wire and_1_out, and_2_out, comparator_1_eq, comparator_1_gt, comparator_1_lt, comparator_2_gt,
       comparator_2_lt, comparator_3_eq, comparator_3_gt, comparator_3_lt, or_1_out;
  wire [15:0] subtractor_1_out;

  Comparator #(.width(16)) comparator_1 (
    .a(IN_A), .b({16{1'b0}}), .gt(comparator_1_gt), .eq(comparator_1_eq), .lt(comparator_1_lt));
  Comparator #(.width(16)) comparator_2 (
    .a(IN_B), .b({16{1'b0}}), .gt(comparator_2_gt), .lt(comparator_2_lt));  // open: eq
  and and_1 (and_1_out, comparator_2_lt, or_1_out, comparator_3_gt);
  or or_1 (or_1_out, comparator_1_eq, comparator_1_gt);
  and and_2 (and_2_out, comparator_2_gt, comparator_1_lt, comparator_3_lt);
  or or_2 (OVF, and_1_out, and_2_out);
  Multiplexer #(.select(2), .width(16), .enable("false")) multiplexer_1 (
    .in0({16{1'b0}}), .in1(IN_A), .in2(IN_B), .in3(subtractor_1_out), .out(OUT), .sel({ENB, ENA}));
  Subtractor #(.width(16)) subtractor_1 (.a(IN_A), .b(IN_B), .out(subtractor_1_out));  // open: bin, bout
  Multiplexer #(.select(2), .enable("false")) multiplexer_2 (
    .in0(1'b0), .in1(comparator_3_gt), .in2(comparator_3_gt), .in3(comparator_3_gt), .out(SGN),
    .sel({ENB, ENA}));
  Comparator #(.width(16)) comparator_3 (
    .a({16{1'b0}}), .b(OUT), .gt(comparator_3_gt), .eq(comparator_3_eq), .lt(comparator_3_lt));
  Multiplexer #(.select(2), .enable("false")) multiplexer_3 (
    .in0(1'b1), .in1(comparator_3_eq), .in2(comparator_3_eq), .in3(comparator_3_eq), .out(ZERO),
    .sel({ENB, ENA}));
endmodule

// ALU IN-MUX
module ALU_Input_MUX (
  input  [15:0] AREG,
  input  [15:0] DATA,
  input  [15:0] ZERO,
  input  [15:0] BREG,
  input  [2:0] SEL,
  output [15:0] L,
  output [15:0] R
);

  Multiplexer #(.select(3), .width(16), .enable("false")) multiplexer_1 (
    .in0(ZERO), .in1(AREG), .in2(AREG), .in3(AREG), .in4(BREG), .in5(DATA), .in6(BREG), .in7(BREG), .out(L),
    .sel(SEL));
  Multiplexer #(.select(3), .width(16), .enable("false")) multiplexer_2 (
    .in0(ZERO), .in1(ZERO), .in2(BREG), .in3(DATA), .in4(DATA), .in5(ZERO), .in6(ZERO), .in7(AREG), .out(R),
    .sel(SEL));
endmodule

// AREG
module ALU_REG_A_MUX (
  input  [15:0] Data,
  input  CLK,
  input  [3:0] WSEL,
  input  [3:0] RSEL,
  input  [15:0] BUS_INPUT_B,
  output [15:0] Output,
  output [15:0] BUS_Output_A,
  output [15:0] BUS_Output_B
);

  wire decoder_1_out0, decoder_1_out1, decoder_1_out2, decoder_1_out3, decoder_1_out4, decoder_1_out5,
       decoder_1_out6, decoder_1_out7, decoder_1_out8, decoder_1_out9, decoder_1_out10, decoder_1_out11,
       decoder_1_out12, decoder_1_out13, decoder_1_out14, decoder_1_out15;
  wire [15:0] REG0_q, REG1_q, REG2_q, REG3_q, REG4_q, REG5_q, REG6_q, REG7_q, REG8_q, REG9_q, REG10_q,
       REG11_q, REG12_q, REG13_q, REG14_q, REG15_q;

  Decoder #(.select(4)) decoder_1 (
    .out0(decoder_1_out0), .out1(decoder_1_out1), .out2(decoder_1_out2), .out3(decoder_1_out3),
    .out4(decoder_1_out4), .out5(decoder_1_out5), .out6(decoder_1_out6), .out7(decoder_1_out7),
    .out8(decoder_1_out8), .out9(decoder_1_out9), .out10(decoder_1_out10), .out11(decoder_1_out11),
    .out12(decoder_1_out12), .out13(decoder_1_out13), .out14(decoder_1_out14), .out15(decoder_1_out15),
    .sel(WSEL));  // open: en
  Register #(.width(16)) REG0 (.D(Data), .en(decoder_1_out0), .Q(REG0_q), .clk(CLK));  // open: clr
  Register #(.width(16)) REG15 (.D(Data), .en(decoder_1_out15), .Q(REG15_q), .clk(CLK));  // open: clr
  Register #(.width(16)) REG1 (.D(Data), .en(decoder_1_out1), .Q(REG1_q), .clk(CLK));  // open: clr
  Register #(.width(16)) REG14 (.D(Data), .en(decoder_1_out14), .Q(REG14_q), .clk(CLK));  // open: clr
  Register #(.width(16)) REG2 (.D(Data), .en(decoder_1_out2), .Q(REG2_q), .clk(CLK));  // open: clr
  Register #(.width(16)) REG13 (.D(Data), .en(decoder_1_out13), .Q(REG13_q), .clk(CLK));  // open: clr
  Register #(.width(16)) REG3 (.D(Data), .en(decoder_1_out3), .Q(REG3_q), .clk(CLK));  // open: clr
  Register #(.width(16)) REG12 (.D(Data), .en(decoder_1_out12), .Q(REG12_q), .clk(CLK));  // open: clr
  Register #(.width(16)) REG4 (.D(Data), .en(decoder_1_out4), .Q(REG4_q), .clk(CLK));  // open: clr
  Register #(.width(16)) REG11 (.D(Data), .en(decoder_1_out11), .Q(REG11_q), .clk(CLK));  // open: clr
  Register #(.width(16)) REG5 (.D(Data), .en(decoder_1_out5), .Q(REG5_q), .clk(CLK));  // open: clr
  Register #(.width(16)) REG10 (.D(Data), .en(decoder_1_out10), .Q(REG10_q), .clk(CLK));  // open: clr
  Register #(.width(16)) REG6 (.D(Data), .en(decoder_1_out6), .Q(REG6_q), .clk(CLK));  // open: clr
  Register #(.width(16)) REG9 (.D(Data), .en(decoder_1_out9), .Q(REG9_q), .clk(CLK));  // open: clr
  Register #(.width(16)) REG7 (.D(Data), .en(decoder_1_out7), .Q(REG7_q), .clk(CLK));  // open: clr
  Register #(.width(16)) REG8 (.D(Data), .en(decoder_1_out8), .Q(REG8_q), .clk(CLK));  // open: clr
  Multiplexer #(.select(4), .width(16)) multiplexer_1 (
    .in0(REG0_q), .in1(REG1_q), .in2(REG2_q), .in3(REG3_q), .in4(REG4_q), .in5(REG5_q), .in6(REG6_q),
    .in7(REG7_q), .in8(REG8_q), .in9(REG9_q), .in10(REG10_q), .in11(REG11_q), .in12(REG12_q), .in13(REG13_q),
    .in14(REG14_q), .in15(REG15_q), .out(BUS_Output_A), .sel(RSEL));  // open: en

  assign BUS_Output_B = BUS_INPUT_B;
  assign Output = BUS_Output_A;
endmodule

// BREG
module ALU_REG_B_MUX (
  input  MOD_REG0_ENB,
  input  [15:0] MOD,
  input  [15:0] Data,
  input  CLK,
  input  [3:0] WSEL,
  input  [3:0] RSEL,
  output [15:0] Output,
  output [15:0] BUS_Output
);

  wire decoder_1_out0, decoder_1_out1, decoder_1_out2, decoder_1_out3, decoder_1_out4, decoder_1_out5,
       decoder_1_out6, decoder_1_out7, decoder_1_out8, decoder_1_out9, decoder_1_out10, decoder_1_out11,
       decoder_1_out12, decoder_1_out13, decoder_1_out14, decoder_1_out15;
  wire [15:0] REG0_q, REG1_q, REG2_q, REG3_q, REG4_q, REG5_q, REG6_q, REG7_q, REG8_q, REG9_q, REG10_q,
       REG11_q, REG12_q, REG13_q, REG14_q, REG15_q;

  Decoder #(.select(4)) decoder_1 (
    .out0(decoder_1_out0), .out1(decoder_1_out1), .out2(decoder_1_out2), .out3(decoder_1_out3),
    .out4(decoder_1_out4), .out5(decoder_1_out5), .out6(decoder_1_out6), .out7(decoder_1_out7),
    .out8(decoder_1_out8), .out9(decoder_1_out9), .out10(decoder_1_out10), .out11(decoder_1_out11),
    .out12(decoder_1_out12), .out13(decoder_1_out13), .out14(decoder_1_out14), .out15(decoder_1_out15),
    .sel(WSEL));  // open: en
  LED led_1 (.in(decoder_1_out0));
  Register #(.width(16), .trigger("falling")) REG0 (.D(MOD), .en(MOD_REG0_ENB), .Q(REG0_q), .clk(CLK));  // open: clr
  Register #(.width(16)) REG15 (.D(Data), .en(decoder_1_out15), .Q(REG15_q), .clk(CLK));  // open: clr
  Register #(.width(16)) REG1 (.D(Data), .en(decoder_1_out1), .Q(REG1_q), .clk(CLK));  // open: clr
  Register #(.width(16)) REG14 (.D(Data), .en(decoder_1_out14), .Q(REG14_q), .clk(CLK));  // open: clr
  Register #(.width(16)) REG2 (.D(Data), .en(decoder_1_out2), .Q(REG2_q), .clk(CLK));  // open: clr
  Register #(.width(16)) REG13 (.D(Data), .en(decoder_1_out13), .Q(REG13_q), .clk(CLK));  // open: clr
  Register #(.width(16)) REG3 (.D(Data), .en(decoder_1_out3), .Q(REG3_q), .clk(CLK));  // open: clr
  Register #(.width(16)) REG12 (.D(Data), .en(decoder_1_out12), .Q(REG12_q), .clk(CLK));  // open: clr
  Register #(.width(16)) REG4 (.D(Data), .en(decoder_1_out4), .Q(REG4_q), .clk(CLK));  // open: clr
  Register #(.width(16)) REG11 (.D(Data), .en(decoder_1_out11), .Q(REG11_q), .clk(CLK));  // open: clr
  Register #(.width(16)) REG5 (.D(Data), .en(decoder_1_out5), .Q(REG5_q), .clk(CLK));  // open: clr
  Register #(.width(16)) REG10 (.D(Data), .en(decoder_1_out10), .Q(REG10_q), .clk(CLK));  // open: clr
  Register #(.width(16)) REG6 (.D(Data), .en(decoder_1_out6), .Q(REG6_q), .clk(CLK));  // open: clr
  Register #(.width(16)) REG9 (.D(Data), .en(decoder_1_out9), .Q(REG9_q), .clk(CLK));  // open: clr
  Register #(.width(16)) REG7 (.D(Data), .en(decoder_1_out7), .Q(REG7_q), .clk(CLK));  // open: clr
  Register #(.width(16)) REG8 (.D(Data), .en(decoder_1_out8), .Q(REG8_q), .clk(CLK));  // open: clr
  Multiplexer #(.select(4), .width(16)) multiplexer_1 (
    .in0(REG0_q), .in1(REG1_q), .in2(REG2_q), .in3(REG3_q), .in4(REG4_q), .in5(REG5_q), .in6(REG6_q),
    .in7(REG7_q), .in8(REG8_q), .in9(REG9_q), .in10(REG10_q), .in11(REG11_q), .in12(REG12_q), .in13(REG13_q),
    .in14(REG14_q), .in15(REG15_q), .out(BUS_Output), .sel(RSEL));  // open: en

  assign Output = BUS_Output;
endmodule

// FUNC
module ALU_FUNC_MUX (
  input  [5:0] FUNC,
  output WSELA,
  output WSELB,
  output ENA,
  output ENB,
  output Y_MUX,
  output F3,
  output F2,
  output F1,
  output F0
);

  wire and_1_out, and_2_out, and_3_out, and_4_out, and_5_out, and_6_out, or_3_out, or_4_out;

  and and_1 (and_1_out, ~FUNC[1], FUNC[3]);  // AND_Gate
  and and_2 (and_2_out, ~FUNC[1], ~FUNC[3], FUNC[4]);  // AND_Gate
  or or_1 (WSELA, and_1_out, and_2_out, and_3_out);
  and and_3 (and_3_out, ~FUNC[1], FUNC[2], ~FUNC[3], ~FUNC[4]);  // AND_Gate
  and and_4 (and_4_out, FUNC[1], FUNC[4]);
  and and_5 (and_5_out, FUNC[1], FUNC[3]);
  and and_6 (and_6_out, FUNC[1], FUNC[2], ~FUNC[4]);  // AND_Gate
  or or_2 (WSELB, and_4_out, and_6_out, and_5_out);
  or or_3 (or_3_out, FUNC[0], FUNC[1], FUNC[2], FUNC[3], FUNC[4]);
  and and_7 (ENA, or_3_out, or_4_out);
  or or_4 (or_4_out, ~FUNC[0], ~FUNC[1], FUNC[2], FUNC[3], FUNC[4]);  // OR_Gate
  or or_5 (ENB, FUNC[1], FUNC[2], FUNC[3], FUNC[4]);

  assign F0 = FUNC[2];
  assign F1 = FUNC[3];
  assign F2 = FUNC[4];
  assign F3 = FUNC[5];
  assign Y_MUX = FUNC[0];
endmodule

// Y-MUX
module ALU_Y_MUX (
  input  BUS_SEL,
  input  ENB_SEL,
  input  CLK,
  input  [15:0] DATA,
  output [15:0] DBUS,
  output [15:0] ABUS
);

  wire not_1_out, not_2_out, not_3_out;
  wire [15:0] demultiplexer_2_out0, demultiplexer_2_out1;

  not not_1 (not_1_out, not_2_out);
  not not_2 (not_2_out, CLK);
  not not_3 (not_3_out, BUS_SEL);
  Demultiplexer #(.width(16)) demultiplexer_1 (
    .out0(DBUS), .in(demultiplexer_2_out0), .sel(BUS_SEL), .en(not_3_out));  // open: out1
  Demultiplexer #(.width(16)) demultiplexer_2 (
    .out0(demultiplexer_2_out0), .out1(demultiplexer_2_out1), .in(DATA), .sel(BUS_SEL), .en(ENB_SEL));
  Register #(.width(16)) register_1 (.clr(not_1_out));  // open: D, en, Q, clk
  Demultiplexer #(.width(16)) demultiplexer_3 (
    .out1(ABUS), .in(demultiplexer_2_out1), .sel(BUS_SEL), .en(BUS_SEL));  // open: out0
endmodule

// K-MUX
module ALU_K_MUX (
  input  [15:0] DATABUS,
  input  [15:0] CONST,
  input  in_3,
  output [15:0] K_INPUT
);

  Multiplexer #(.width(16), .enable("false")) multiplexer_1 (.in0(DATABUS), .in1(CONST), .out(K_INPUT), .sel(in_3));
endmodule

// MUL
module ALU_MUL (
  input  A15,
  input  A14,
  input  A13,
  input  A12,
  input  A11,
  input  A10,
  input  A9,
  input  A8,
  input  A7,
  input  A6,
  input  A5,
  input  A4,
  input  A3,
  input  A2,
  input  A1,
  input  A0,
  input  B0,
  input  B1,
  input  B2,
  input  B3,
  input  B4,
  input  B5,
  input  B6,
  input  B7,
  input  B8,
  input  B9,
  input  B10,
  input  B11,
  input  B12,
  input  B13,
  input  B14,
  input  B15,
  output SGN,
  output ZERO,
  output [15:0] OUTPUT,
  output OVF
);

  wire adder_1_cout, adder_2_cout, adder_3_cout, adder_5_cout, adder_6_cout, adder_7_cout, adder_8_cout,
       adder_9_cout, adder_10_cout, adder_11_cout, adder_12_cout, adder_13_cout, adder_14_cout,
       adder_15_cout, adder_16_cout, and_1_out, and_2_out, and_3_out, and_4_out, and_5_out, comparator_2_eq,
       comparator_2_gt, comparator_2_lt, comparator_3_eq, comparator_3_gt, comparator_3_lt, comparator_4_eq,
       comparator_4_gt, comparator_4_lt, not_1_out, not_2_out, not_3_out, not_4_out, not_5_out, not_6_out,
       not_7_out;
  wire [31:0] adder_1_out, adder_2_out, adder_3_out, adder_5_out, adder_6_out, adder_7_out, adder_8_out,
       adder_9_out, adder_10_out, adder_11_out, adder_12_out, adder_13_out, adder_14_out, adder_15_out,
       adder_16_out, multiplexer_1_out, multiplexer_2_out, multiplexer_3_out, multiplexer_4_out,
       multiplexer_5_out, multiplexer_6_out, multiplexer_7_out, multiplexer_8_out, multiplexer_9_out,
       multiplexer_10_out, multiplexer_11_out, multiplexer_12_out, multiplexer_13_out, multiplexer_14_out,
       multiplexer_15_out, multiplexer_16_out;
  wire [31:16] adder_4_out;

  Multiplexer #(.width(32), .enable("false")) multiplexer_1 (
    .in0({32{1'b0}}),
    .in1({{8{1'b0}}, A15, A14, A13, A12, A11, A10, A9, A8, A7, A6, A5, A4, A3, A2, A1, A0, {8{1'b0}}}),
    .out(multiplexer_1_out), .sel(B8));
  Multiplexer #(.width(32), .enable("false")) multiplexer_2 (
    .in0({{7{1'b0}}, A15, A14, A13, A12, A11, A10, A9, A8, A7, A6, A5, A4, A3, A2, A1, A0, {9{1'b0}}}),
    .in1({32{1'b0}}), .out(multiplexer_2_out), .sel(not_1_out));
  not not_1 (not_1_out, B9);
  Multiplexer #(.width(32), .enable("false")) multiplexer_3 (
    .in0({32{1'b0}}),
    .in1({{9{1'b0}}, A15, A14, A13, A12, A11, A10, A9, A8, A7, A6, A5, A4, A3, A2, A1, A0, {7{1'b0}}}),
    .out(multiplexer_3_out), .sel(B7));
  Multiplexer #(.width(32), .enable("false")) multiplexer_4 (
    .in0({{6{1'b0}}, A15, A14, A13, A12, A11, A10, A9, A8, A7, A6, A5, A4, A3, A2, A1, A0, {10{1'b0}}}),
    .in1({32{1'b0}}), .out(multiplexer_4_out), .sel(not_2_out));
  not not_2 (not_2_out, B10);
  not not_3 (not_3_out, B11);
  Multiplexer #(.width(32), .enable("false")) multiplexer_5 (
    .in0({32{1'b0}}),
    .in1({{11{1'b0}}, A15, A14, A13, A12, A11, A10, A9, A8, A7, A6, A5, A4, A3, A2, A1, A0, {5{1'b0}}}),
    .out(multiplexer_5_out), .sel(B5));
  Multiplexer #(.width(32), .enable("false")) multiplexer_6 (
    .in0({32{1'b0}}),
    .in1({{10{1'b0}}, A15, A14, A13, A12, A11, A10, A9, A8, A7, A6, A5, A4, A3, A2, A1, A0, {6{1'b0}}}),
    .out(multiplexer_6_out), .sel(B6));
  Multiplexer #(.width(32), .enable("false")) multiplexer_7 (
    .in0({{5{1'b0}}, A15, A14, A13, A12, A11, A10, A9, A8, A7, A6, A5, A4, A3, A2, A1, A0, {11{1'b0}}}),
    .in1({32{1'b0}}), .out(multiplexer_7_out), .sel(not_3_out));
  Multiplexer #(.width(32), .enable("false")) multiplexer_8 (
    .in0({4'b0000, A15, A14, A13, A12, A11, A10, A9, A8, A7, A6, A5, A4, A3, A2, A1, A0, {12{1'b0}}}),
    .in1({32{1'b0}}), .out(multiplexer_8_out), .sel(not_4_out));
  not not_4 (not_4_out, B12);
  Multiplexer #(.width(32), .enable("false")) multiplexer_9 (
    .in0({32{1'b0}}),
    .in1({{12{1'b0}}, A15, A14, A13, A12, A11, A10, A9, A8, A7, A6, A5, A4, A3, A2, A1, A0, 4'b0000}),
    .out(multiplexer_9_out), .sel(B4));
  Multiplexer #(.width(32), .enable("false")) multiplexer_10 (
    .in0({3'b000, A15, A14, A13, A12, A11, A10, A9, A8, A7, A6, A5, A4, A3, A2, A1, A0, {13{1'b0}}}),
    .in1({32{1'b0}}), .out(multiplexer_10_out), .sel(not_5_out));
  not not_5 (not_5_out, B13);
  not not_6 (not_6_out, B14);
  Multiplexer #(.width(32), .enable("false")) multiplexer_11 (
    .in0({32{1'b0}}),
    .in1({{14{1'b0}}, A15, A14, A13, A12, A11, A10, A9, A8, A7, A6, A5, A4, A3, A2, A1, A0, 2'b00}),
    .out(multiplexer_11_out), .sel(B2));
  Multiplexer #(.width(32), .enable("false")) multiplexer_12 (
    .in0({32{1'b0}}),
    .in1({{13{1'b0}}, A15, A14, A13, A12, A11, A10, A9, A8, A7, A6, A5, A4, A3, A2, A1, A0, 3'b000}),
    .out(multiplexer_12_out), .sel(B3));
  Multiplexer #(.width(32), .enable("false")) multiplexer_13 (
    .in0({2'b00, A15, A14, A13, A12, A11, A10, A9, A8, A7, A6, A5, A4, A3, A2, A1, A0, {14{1'b0}}}),
    .in1({32{1'b0}}), .out(multiplexer_13_out), .sel(not_6_out));
  Multiplexer #(.width(32), .enable("false")) multiplexer_14 (
    .in0({1'b0, A15, A14, A13, A12, A11, A10, A9, A8, A7, A6, A5, A4, A3, A2, A1, A0, {15{1'b0}}}),
    .in1({32{1'b0}}), .out(multiplexer_14_out), .sel(not_7_out));
  not not_7 (not_7_out, B15);
  Multiplexer #(.width(32), .enable("false")) multiplexer_15 (
    .in0({32{1'b0}}),
    .in1({{15{1'b0}}, A15, A14, A13, A12, A11, A10, A9, A8, A7, A6, A5, A4, A3, A2, A1, A0, 1'b0}),
    .out(multiplexer_15_out), .sel(B1));
  Multiplexer #(.width(32), .enable("false")) multiplexer_16 (
    .in0({32{1'b0}}),
    .in1({{16{1'b0}}, A15, A14, A13, A12, A11, A10, A9, A8, A7, A6, A5, A4, A3, A2, A1, A0}),
    .out(multiplexer_16_out), .sel(B0));
  Adder #(.width(32)) adder_1 (
    .a(multiplexer_16_out), .b(multiplexer_15_out), .out(adder_1_out), .cout(adder_1_cout));  // open: cin
  Adder #(.width(32)) adder_2 (
    .a(adder_1_out), .b(multiplexer_11_out), .out(adder_2_out), .cin(adder_1_cout), .cout(adder_2_cout));
  Adder #(.width(32)) adder_3 (
    .a(adder_6_out), .b(multiplexer_14_out), .out(adder_3_out), .cin(adder_6_cout), .cout(adder_3_cout));
  Adder #(.width(32)) adder_4 (
    .a(adder_3_out), .b({32{1'b0}}), .out({adder_4_out, OUTPUT}), .cin(adder_3_cout));  // open: cout
  Adder #(.width(32)) adder_5 (
    .a(adder_2_out), .b(multiplexer_12_out), .out(adder_5_out), .cin(adder_2_cout), .cout(adder_5_cout));
  Adder #(.width(32)) adder_6 (
    .a(adder_8_out), .b(multiplexer_13_out), .out(adder_6_out), .cin(adder_8_cout), .cout(adder_6_cout));
  Adder #(.width(32)) adder_7 (
    .a(adder_5_out), .b(multiplexer_9_out), .out(adder_7_out), .cin(adder_5_cout), .cout(adder_7_cout));
  Adder #(.width(32)) adder_8 (
    .a(adder_12_out), .b(multiplexer_10_out), .out(adder_8_out), .cin(adder_12_cout), .cout(adder_8_cout));
  Adder #(.width(32)) adder_9 (
    .a(adder_7_out), .b(multiplexer_5_out), .out(adder_9_out), .cin(adder_7_cout), .cout(adder_9_cout));
  Adder #(.width(32)) adder_10 (
    .a(adder_9_out), .b(multiplexer_6_out), .out(adder_10_out), .cin(adder_9_cout), .cout(adder_10_cout));
  Adder #(.width(32)) adder_11 (
    .a(adder_14_out), .b(multiplexer_7_out), .out(adder_11_out), .cin(adder_14_cout), .cout(adder_11_cout));
  Adder #(.width(32)) adder_12 (
    .a(adder_11_out), .b(multiplexer_8_out), .out(adder_12_out), .cin(adder_11_cout), .cout(adder_12_cout));
  Adder #(.width(32)) adder_13 (
    .a(adder_10_out), .b(multiplexer_3_out), .out(adder_13_out), .cin(adder_10_cout), .cout(adder_13_cout));
  Adder #(.width(32)) adder_14 (
    .a(adder_16_out), .b(multiplexer_4_out), .out(adder_14_out), .cin(adder_16_cout), .cout(adder_14_cout));
  Comparator #(.width(16)) comparator_1 (.a({16{1'b0}}), .b(OUTPUT), .gt(SGN), .eq(ZERO));  // open: lt
  Comparator #(.width(16)) comparator_2 (
    .a(OUTPUT), .b({16{1'b0}}), .gt(comparator_2_gt), .eq(comparator_2_eq), .lt(comparator_2_lt));
  Comparator #(.width(16)) comparator_3 (
    .a({B15, B14, B13, B12, B11, B10, B9, B8, B7, B6, B5, B4, B3, B2, B1, B0}), .b({16{1'b0}}),
    .gt(comparator_3_gt), .eq(comparator_3_eq), .lt(comparator_3_lt));
  Comparator #(.width(16)) comparator_4 (
    .a({A15, A14, A13, A12, A11, A10, A9, A8, A7, A6, A5, A4, A3, A2, A1, A0}), .b({16{1'b0}}),
    .gt(comparator_4_gt), .eq(comparator_4_eq), .lt(comparator_4_lt));
  Adder #(.width(32)) adder_15 (
    .a(adder_13_out), .b(multiplexer_1_out), .out(adder_15_out), .cin(adder_13_cout), .cout(adder_15_cout));
  Adder #(.width(32)) adder_16 (
    .a(adder_15_out), .b(multiplexer_2_out), .out(adder_16_out), .cin(adder_15_cout), .cout(adder_16_cout));
  and and_1 (and_1_out, comparator_2_eq, ~comparator_3_eq, ~comparator_4_eq);  // AND_Gate
  and and_2 (and_2_out, comparator_3_gt, comparator_2_lt, comparator_4_gt);
  and and_3 (and_3_out, comparator_2_gt, comparator_3_gt, comparator_4_lt);
  and and_4 (and_4_out, comparator_2_gt, comparator_4_lt, comparator_3_gt);
  and and_5 (and_5_out, comparator_2_lt, comparator_3_lt, comparator_4_lt);
  or or_1 (OVF, and_2_out, and_3_out, and_1_out, and_4_out, and_5_out);
endmodule

// DIV
module ALU_DIV (
  input  [15:0] INPUT_A,
  input  [15:0] INPUT_B,
  output OVF,
  output [15:0] MOD,
  output ZERO,
  output SGN,
  output [15:0] DIV_OUTPUT
);

  wire and_1_out, and_2_out, not_33_out, or_1_out, or_2_out;
  wire [1:0] not_37_out, not_51_out;
  wire [14:0] adder_3_out, divider_1_out;
  wire [15:0] adder_1_out, adder_2_out, multiplexer_1_out, multiplexer_2_out, not_20_out, not_30_out,
       not_50_out;

  LED u_SGN (.in(INPUT_A[15]));
  LED led_1 (.in(MOD[15]));
  LED led_2 (.in(MOD[14]));
  Multiplexer #(.width(16), .enable("false")) multiplexer_1 (
    .in0(INPUT_A), .in1(adder_1_out), .out(multiplexer_1_out), .sel(INPUT_A[15]));
  LED led_3 (.in(MOD[10]));
  LED led_4 (.in(MOD[12]));
  LED led_5 (.in(MOD[11]));
  LED led_6 (.in(MOD[13]));
  not not_1 (not_20_out[12], INPUT_A[12]);
  not not_2 (not_20_out[15], INPUT_A[15]);
  not not_3 (not_20_out[10], INPUT_A[10]);
  not not_4 (not_20_out[11], INPUT_A[11]);
  not not_5 (not_20_out[14], INPUT_A[14]);
  not not_6 (not_20_out[13], INPUT_A[13]);
  LED led_7 (.in(MOD[9]));
  LED led_8 (.in(MOD[8]));
  LED led_9 (.in(MOD[6]));
  LED led_10 (.in(MOD[7]));
  not not_7 (not_20_out[8], INPUT_A[8]);
  not not_8 (not_20_out[6], INPUT_A[6]);
  not not_9 (not_20_out[7], INPUT_A[7]);
  not not_10 (not_20_out[9], INPUT_A[9]);
  not not_11 (not_20_out[2], INPUT_A[2]);
  not not_12 (not_20_out[3], INPUT_A[3]);
  not not_13 (not_20_out[4], INPUT_A[4]);
  not not_14 (not_20_out[5], INPUT_A[5]);
  Adder #(.width(16)) adder_1 (.a(not_20_out), .b(16'h1), .out(adder_1_out));  // open: cin, cout
  LED led_11 (.in(MOD[2]));
  LED led_12 (.in(MOD[4]));
  LED led_13 (.in(MOD[3]));
  LED led_14 (.in(MOD[5]));
  not not_15 (not_20_out[1], INPUT_A[1]);
  not not_16 (not_30_out[11], INPUT_B[11]);
  not not_17 (not_30_out[12], INPUT_B[12]);
  not not_18 (not_30_out[15], INPUT_B[15]);
  not not_19 (not_30_out[14], INPUT_B[14]);
  not not_20 (not_20_out[0], INPUT_A[0]);
  not not_21 (not_30_out[13], INPUT_B[13]);
  Divider #(.width(16)) divider_1 (
    .a(multiplexer_1_out), .b(multiplexer_2_out), .out({not_37_out[1], divider_1_out}), .rem(MOD));  // open: upper
  LED led_15 (.in(MOD[0]));
  LED led_16 (.in(MOD[1]));
  not not_22 (not_30_out[4], INPUT_B[4]);
  not not_23 (not_30_out[8], INPUT_B[8]);
  not not_24 (not_30_out[6], INPUT_B[6]);
  not not_25 (not_30_out[7], INPUT_B[7]);
  not not_26 (not_30_out[10], INPUT_B[10]);
  not not_27 (not_30_out[9], INPUT_B[9]);
  not not_28 (not_30_out[3], INPUT_B[3]);
  not not_29 (not_30_out[5], INPUT_B[5]);
  not not_30 (not_30_out[0], INPUT_B[0]);
  not not_31 (not_30_out[2], INPUT_B[2]);
  not not_32 (not_30_out[1], INPUT_B[1]);
  Adder #(.width(16)) adder_2 (.a(not_30_out), .b(16'h1), .out(adder_2_out));  // open: cin, cout
  not not_33 (not_33_out, INPUT_B[15]);
  Multiplexer #(.width(16), .enable("false")) multiplexer_2 (
    .in0(adder_2_out), .in1(INPUT_B), .out(multiplexer_2_out), .sel(not_33_out));
  not not_34 (not_50_out[13], divider_1_out[13]);
  not not_35 (not_50_out[14], divider_1_out[14]);
  not not_36 (not_50_out[15], not_37_out[1]);
  or or_1 (or_1_out, divider_1_out[0], divider_1_out[1], divider_1_out[2], divider_1_out[3], divider_1_out[4], divider_1_out[5], divider_1_out[6], divider_1_out[7], divider_1_out[8], divider_1_out[9], divider_1_out[10], divider_1_out[11], divider_1_out[12], divider_1_out[13], divider_1_out[14], not_37_out[1]);
  not not_37 (not_37_out[0], or_1_out);
  Multiplexer #(.select(2), .width(16), .enable("false")) multiplexer_3 (
    .in0({not_37_out[1], divider_1_out}), .in1({not_51_out[1], adder_3_out}),
    .in2({not_51_out[1], adder_3_out}), .in3({not_37_out[1], divider_1_out}), .out(DIV_OUTPUT),
    .sel({INPUT_B[15], INPUT_A[15]}));
  LED SGN_2 (.in(INPUT_B[15]));
  not not_38 (not_50_out[9], divider_1_out[9]);
  not not_39 (not_50_out[5], divider_1_out[5]);
  not not_40 (not_50_out[6], divider_1_out[6]);
  not not_41 (not_50_out[12], divider_1_out[12]);
  not not_42 (not_50_out[8], divider_1_out[8]);
  not not_43 (not_50_out[11], divider_1_out[11]);
  not not_44 (not_50_out[10], divider_1_out[10]);
  not not_45 (not_50_out[7], divider_1_out[7]);
  not not_46 (not_50_out[1], divider_1_out[1]);
  not not_47 (not_50_out[2], divider_1_out[2]);
  not not_48 (not_50_out[4], divider_1_out[4]);
  not not_49 (not_50_out[3], divider_1_out[3]);
  not not_50 (not_50_out[0], divider_1_out[0]);
  Adder #(.width(16)) adder_3 (.a(not_50_out), .b(16'h1), .out({not_51_out[1], adder_3_out}));  // open: cin, cout
  or or_2 (or_2_out, adder_3_out[0], adder_3_out[1], adder_3_out[2], adder_3_out[3], adder_3_out[4], adder_3_out[5], adder_3_out[6], adder_3_out[7], adder_3_out[8], adder_3_out[9], adder_3_out[10], adder_3_out[11], adder_3_out[12], adder_3_out[13], adder_3_out[14], not_51_out[1]);
  not not_51 (not_51_out[0], or_2_out);
  and and_1 (and_1_out, ~INPUT_A[0], ~INPUT_A[1], ~INPUT_A[2], ~INPUT_A[3], ~INPUT_A[4], ~INPUT_A[5], ~INPUT_A[6], ~INPUT_A[7], ~INPUT_A[9], ~INPUT_A[10], ~INPUT_A[11], ~INPUT_A[12], ~INPUT_A[13], ~INPUT_A[14], INPUT_A[15], ~INPUT_A[8]);  // AND_Gate
  and and_2 (and_2_out, INPUT_B[0], INPUT_B[1], INPUT_B[2], INPUT_B[3], INPUT_B[4], INPUT_B[5], INPUT_B[6], INPUT_B[7], INPUT_B[9], INPUT_B[10], INPUT_B[11], INPUT_B[12], INPUT_B[13], INPUT_B[14], INPUT_B[15], INPUT_B[8]);
  Multiplexer #(.select(2), .width(2), .enable("false")) multiplexer_4 (
    .in0(not_37_out), .in1(not_51_out), .in2(not_51_out), .in3(not_37_out), .out({SGN, ZERO}),
    .sel({INPUT_A[15], INPUT_B[15]}));
  and and_3 (OVF, and_1_out, and_2_out);

  // Notes on the sheet:
  //   MOD
endmodule

// XOR
module ALU_XOR (
  input  [15:0] IN_A,
  input  [15:0] IN_B,
  output SGN,
  output OVF,
  output ZERO,
  output [15:0] OUT_XOR
);

  wire or_1_out;

  xor xor_1 (OUT_XOR[15], IN_A[15], IN_B[15]);
  xor xor_2 (OUT_XOR[13], IN_A[13], IN_B[13]);
  xor xor_3 (OUT_XOR[14], IN_A[14], IN_B[14]);
  xor xor_4 (OUT_XOR[12], IN_A[12], IN_B[12]);
  xor xor_5 (OUT_XOR[11], IN_A[11], IN_B[11]);
  not not_1 (ZERO, or_1_out);
  or or_1 (or_1_out, OUT_XOR[15], OUT_XOR[14], OUT_XOR[13], OUT_XOR[12], OUT_XOR[11], OUT_XOR[10], OUT_XOR[9], OUT_XOR[8], OUT_XOR[7], OUT_XOR[6], OUT_XOR[5], OUT_XOR[4], OUT_XOR[3], OUT_XOR[2], OUT_XOR[1], OUT_XOR[0]);
  xor xor_6 (OUT_XOR[10], IN_A[10], IN_B[10]);
  xor xor_7 (OUT_XOR[9], IN_A[9], IN_B[9]);
  xor xor_8 (OUT_XOR[8], IN_A[8], IN_B[8]);
  xor xor_9 (OUT_XOR[7], IN_A[7], IN_B[7]);
  xor xor_10 (OUT_XOR[6], IN_A[6], IN_B[6]);
  xor xor_11 (OUT_XOR[5], IN_A[5], IN_B[5]);
  xor xor_12 (OUT_XOR[3], IN_A[3], IN_B[3]);
  xor xor_13 (OUT_XOR[4], IN_A[4], IN_B[4]);
  xor xor_14 (OUT_XOR[1], IN_A[1], IN_B[1]);
  xor xor_15 (OUT_XOR[2], IN_A[2], IN_B[2]);
  xor xor_16 (OUT_XOR[0], IN_A[0], IN_B[0]);

  assign OVF = 1'b0;
  assign SGN = OUT_XOR[15];
endmodule

// MUX
module ALU_XA_MUX (
  input  in_1,
  input  in_2,
  input  in_3,
  input  in_4,
  input  in_5,
  input  in_6,
  input  in_7,
  input  in_8,
  input  MUX,
  output out_10,
  output out_11,
  output out_12,
  output out_13
);

  wire and_1_out, and_2_out, and_3_out, and_4_out, and_5_out, and_6_out, and_7_out, and_8_out;

  and and_1 (and_1_out, ~MUX, in_1);  // AND_Gate
  and and_2 (and_2_out, ~MUX, in_3);  // AND_Gate
  and and_3 (and_3_out, ~MUX, in_4);  // AND_Gate
  and and_4 (and_4_out, ~MUX, in_2);  // AND_Gate
  or or_1 (out_10, and_1_out, and_5_out);
  and and_5 (and_5_out, MUX, in_5);
  and and_6 (and_6_out, MUX, in_6);
  or or_2 (out_13, and_3_out, and_7_out);
  or or_3 (out_12, and_2_out, and_8_out);
  or or_4 (out_11, and_4_out, and_6_out);
  and and_7 (and_7_out, MUX, in_8);
  and and_8 (and_8_out, MUX, in_7);
endmodule

// MUX
module ALU_XB_MUX (
  input  in_1,
  input  in_2,
  input  in_3,
  input  in_4,
  input  in_5,
  input  in_6,
  input  in_7,
  input  in_8,
  input  MUX,
  output out_10,
  output out_11,
  output out_12,
  output out_13
);

  wire and_1_out, and_2_out, and_3_out, and_4_out, and_5_out, and_6_out, and_7_out, and_8_out;

  and and_1 (and_1_out, ~MUX, in_1);  // AND_Gate
  and and_2 (and_2_out, ~MUX, in_2);  // AND_Gate
  and and_3 (and_3_out, ~MUX, in_3);  // AND_Gate
  and and_4 (and_4_out, ~MUX, in_4);  // AND_Gate
  or or_1 (out_10, and_1_out, and_6_out);
  and and_5 (and_5_out, MUX, in_6);
  and and_6 (and_6_out, MUX, in_5);
  or or_2 (out_12, and_3_out, and_7_out);
  or or_3 (out_11, and_2_out, and_5_out);
  or or_4 (out_13, and_4_out, and_8_out);
  and and_7 (and_7_out, MUX, in_7);
  and and_8 (and_8_out, MUX, in_8);
endmodule

// MUX
module ALU_F_FUN_MUX (
  input  F2,
  input  F1,
  input  F0,
  output SUB,
  output FA1,
  output FA0
);

  wire and_1_out, and_3_out, and_4_out;

  and and_1 (and_1_out, F0, F1, F2);
  and and_2 (SUB, ~F0, F1, ~F2);  // AND_Gate
  or or_1 (FA1, and_1_out, and_4_out);
  or or_2 (FA0, and_4_out, and_3_out);
  and and_3 (and_3_out, ~F0, F1, F2);  // AND_Gate
  and and_4 (and_4_out, F0, ~F1, ~F2);  // AND_Gate
endmodule

module IR_Instruction_Register (
  input  [15:0] DBUS,
  input  IR_LD,
  input  CLK,
  input  IR_RES,
  output [3:0] _15_12,
  output [3:0] _11_8,
  output [3:0] _7_4,
  output [3:0] _3_0,
  output [15:0] IREG
);

  Register #(.width(16), .trigger("falling")) Instruction_Register (
    .D(DBUS), .en(IR_LD), .Q({_15_12, _11_8, _7_4, _3_0}), .clk(CLK), .clr(IR_RES));

  assign IREG = {_15_12, _11_8, _7_4, _3_0};
endmodule

// PC
module PC_Controler (
  input  BUS_SEL,
  input  ENB_OUT,
  input  [15:0] PC_IN,
  output [15:0] DBUS,
  output [15:0] ABUS
);

  wire not_1_out, not_2_out;
  wire [15:0] demultiplexer_3_out0, demultiplexer_3_out1;

  not not_1 (not_1_out, not_2_out);
  Demultiplexer #(.width(16)) demultiplexer_1 (
    .out0(DBUS), .in(demultiplexer_3_out0), .sel(not_2_out), .en(not_1_out));  // open: out1
  Demultiplexer #(.width(16)) demultiplexer_2 (
    .out1(ABUS), .in(demultiplexer_3_out1), .sel(not_2_out), .en(not_2_out));  // open: out0
  Demultiplexer #(.width(16)) demultiplexer_3 (
    .out0(demultiplexer_3_out0), .out1(demultiplexer_3_out1), .in(PC_IN), .sel(not_2_out), .en(ENB_OUT));
  not not_2 (not_2_out, BUS_SEL);
endmodule

// MPS
module \CU_µCS  (
  input  [15:0] \µAddress ,
  input  MPS_ENABLE,
  output [31:0] \µIR_1 ,
  output [31:0] \µIR_2 ,
  output [31:0] \µIR_3 
);

  ROM #(.addrWidth(16), .dataWidth(32)) rom_1 (.addr(\µAddress ), .data(\µIR_1 ), .sel(MPS_ENABLE));
  ROM #(.addrWidth(16), .dataWidth(32)) rom_2 (.addr(\µAddress ), .data(\µIR_2 ), .sel(MPS_ENABLE));
  ROM #(.addrWidth(16), .dataWidth(32)) rom_3 (.addr(\µAddress ), .data(\µIR_3 ), .sel(MPS_ENABLE));

  // Notes on the sheet:
  //   contents of rom_1 (hex, n*v repeats v):
  //   8b480000 8140001 8140001 8d140000 8140000 8140000 8b140001 8b140001 8b140000 8b180000 90180000
  //   30180000 50140000 30180000 50180000 98180000 90140000 30180000 50180000 98180000 90140000 8b180000
  //   40180000 88140000 10*8140001 8140092 a140000 8d140000 5*8140001 8b140000 8b140000 4*8140001 90180000
  //   30180000 50140000 90180000 30180000 50140000 8140000 8b180000 91980000 30180000 50180000 c140000
  //   30180000 50180000 9c180000 90140000 8140000 40180000 50140000 30180000 60140000 40180000 90180000
  //   30180000 50140000 30180000 50180000 98180000 60140000 8b180000 30180001 50140000 30180000 8b180001
  //   50140000 8140156 a140000 8d140000 8140162 a140000 8d140000 814016e a140000 8d140000 814017a a140000
  //   8d140000 4*8b140001 8180000 8180000 8180000 8140000 8b140001 8b140001 8b180000 80140000 8b180000
  //   80140000 8b180000 8b180000 80140000 8b180000 8b180000 80140000 8140001 8140001 8140001
  //   contents of rom_2 (hex, n*v repeats v):
  //   0 18900 20d00 0 8c00 30800 18800 20c00 28800 f828800 f808a00 8028800 8019300 8028800 8018b00 28800
  //   8028b00 8028800 8018b00 28c00 428b00 7e8c00 7e0c00 7e8800 13000 13400 11800 11c00 11000 39000 39400
  //   11400 10800 10c00 20000000 0 0 10400 12800 12c00 b800 33c00 28800 28c00 12000 3a000 3a400 12400 0
  //   8028800 8019300 0 8028800 8019300 8800 f828800 0 8028800 8019300 f800000 8028800 8018b00 0 428b00
  //   30c00 7e8c00 7f0e00 7e8c00 7f0e00 7e8c00 7f0e00 8028800 8019300 8028800 8018b00 7e8c00 7f0e00
  //   f828800 f818800 f808a00 f828800 f819000 f808a00 30000000 5*0 a0000000 0 0 80000000 0 0 18400 20400
  //   19800 21c00 7c8c00 30800 fff0800 f808c00 1a000 22400 7e8c00 7f0e00 f828800 f808a00 7d8c00 f828800
  //   ffc8a00 7d9400 f828800 ffc8a00 14000 14400 8800
  //   contents of rom_3 (hex, n*v repeats v):
  //   0 1002000 1002000 0 0 2000 2000 2000 3000 2000 2000 0 1000000 2000 1002000 2000 0 2000 1002000 2000
  //   0 2000 2000 702000 10*2000 0 0 0 11*2000 402000 0 1000000 502000 0 1000000 3000 2000 0 0 1000000
  //   402000 2000 1002000 0 0 3000 6*2000 0 1000000 2000 1002000 8*2000 12*0 4*2000 4*0 2000 2000 2000
  //   600000 2000 700000 0 2000 700000 0 2000 700000 2000 2000 16000
endmodule
// Control Unit
module CU_Control_Unit (
  input  [7:0] BUS_ADDRESS,
  input  ENB,
  input  DSEL,
  input  CCEN,
  input  CLK,
  input  [1:0] ADDRSSEL,
  input  [15:0] CONST,
  output [7:0] \µPROG ,
  output [15:0] MPS
);

  wire and_1_out, \cu_instruction_pla_1_µir_reset , not_1_out;
  wire [7:0] adder_2_out, counter_1_q;
  wire [15:0] adder_1_out, multiplexer_1_out, rom_1_data, \µPC_q ;

  Adder #(.width(16)) adder_1 (.a(16'h1), .b(MPS), .out(adder_1_out));  // open: cin, cout
  Register #(.width(16)) \u_µPC  (
    .D(adder_1_out), .Q(\µPC_q ), .clk(CLK), .clr(\cu_instruction_pla_1_µir_reset ));  // open: en
  ROM #(.dataWidth(16)) rom_1 (.addr(BUS_ADDRESS), .data(rom_1_data), .sel(ENB));
  Multiplexer #(.width(16), .enable("false")) multiplexer_1 (
    .in0(rom_1_data), .in1(CONST), .out(multiplexer_1_out), .sel(DSEL));
  CU_Instruction_PLA cu_instruction_pla_1 (
    .CCEN(CCEN), .CU_Instruction(ADDRSSEL), .\µIR_RESET (\cu_instruction_pla_1_µir_reset ),
    .D_INPUT(multiplexer_1_out), .\µIR (\µPC_q ), .Y_OUTPUT(MPS));
  Counter #(.trigger("falling")) counter_1 (
    .count(and_1_out), .Q(counter_1_q), .clk(CLK), .clr(not_1_out));  // open: load, D, carry
  and and_1 (and_1_out, ADDRSSEL[0], ADDRSSEL[1]);
  not not_1 (not_1_out, and_1_out);
  Adder adder_2 (.a(8'h1), .b(counter_1_q), .out(adder_2_out));  // open: cin, cout
  Transistor #(.\type ("n"), .width(8)) transistor_1 (.in(adder_2_out), .out(\µPROG ), .gate(ENB));

  // Notes on the sheet:
  //   MAPPING-PROM
  //   contents of rom_1 (hex, n*v repeats v):
  //   0 1 2 3 4 5 6 7 8 9 d 11 15 18 19 1a 1b 1c 1d 1e 1f 20 21 22 25 26 27 28 29 2a 2b 2c 2d 2e 2f 30 33
  //   36 37 3c 40 41 43 45 49 4d 50 53 56 59 5c 5f 60 61 62 63 67 68 69 6b 6d 70 73 74 75
endmodule

// Condition Unit
module CU_Condition_Unit (
  input  [2:0] FLAGS,
  input  CLK,
  input  \µSR_ENABLE ,
  input  CCEN,
  input  [3:0] FLAG_SEL,
  output SGN,
  output ZERO,
  output OVF,
  output CCEN_2
);

  wire and_1_out, multiplexer_2_out, not_1_out, not_2_out, not_3_out, not_4_out, not_5_out, not_6_out,
       not_7_out, not_8_out, not_9_out, not_10_out, xnor_1_out;

  Multiplexer #(.enable("false")) multiplexer_1 (.in0(multiplexer_2_out), .in1(1'b1), .out(CCEN_2), .sel(not_1_out));
  not not_1 (not_1_out, CCEN);
  Multiplexer #(.select(4), .enable("false")) multiplexer_2 (
    .in0(OVF), .in1(not_2_out), .in2(ZERO), .in3(not_3_out), .in4(SGN), .in5(not_4_out), .in6(and_1_out),
    .in7(xnor_1_out), .in8(not_5_out), .in9(xnor_1_out), .in10(not_6_out), .in11(and_1_out), .in12(ZERO),
    .in13(not_7_out), .in14(not_8_out), .in15(not_9_out), .out(multiplexer_2_out), .sel(FLAG_SEL));
  and and_1 (and_1_out, xnor_1_out, not_10_out);
  not not_2 (not_2_out, OVF);
  not not_3 (not_3_out, ZERO);
  not not_4 (not_4_out, SGN);
  not not_5 (not_5_out, xnor_1_out);
  not not_6 (not_6_out, and_1_out);
  not not_7 (not_7_out, ZERO);
  not not_8 (not_8_out, and_1_out);
  not not_9 (not_9_out, xnor_1_out);
  xnor xnor_1 (xnor_1_out, OVF, SGN);
  not not_10 (not_10_out, ZERO);
  Register #(.width(3), .trigger("falling")) Status_Register (
    .D(FLAGS), .en(\µSR_ENABLE ), .Q({SGN, ZERO, OVF}), .clk(CLK));  // open: clr

  // Notes on the sheet:
  //   OVF
  //   ZERO
  //   SGN
endmodule

// PLA
module CU_Instruction_PLA (
  input  [15:0] D_INPUT,
  input  [15:0] \µIR ,
  input  CCEN,
  input  [1:0] CU_Instruction,
  output \µIR_RESET ,
  output [15:0] Y_OUTPUT
);

  wire not_1_out;
  wire [15:0] multiplexer_1_out;

  not not_1 (not_1_out, CCEN);
  Multiplexer #(.width(16), .enable("false")) multiplexer_1 (
    .in0(D_INPUT), .in1(\µIR ), .out(multiplexer_1_out), .sel(not_1_out));
  Multiplexer #(.select(2), .width(16), .enable("false")) multiplexer_2 (
    .in0({16{1'b0}}), .in1(D_INPUT), .in2(multiplexer_1_out), .in3(\µIR ), .out(Y_OUTPUT),
    .sel(CU_Instruction));
  and and_1 (\µIR_RESET , ~CU_Instruction[0], ~CU_Instruction[1]);  // AND_Gate
endmodule

// RB-MUX
module REG_BUS_Controler (
  input  BUS_SEL,
  input  ENB_OUT,
  input  [15:0] REGA,
  input  [15:0] REGB,
  input  REG_SEL,
  output [15:0] DBUS,
  output [15:0] ABUS
);

  wire not_1_out;
  wire [15:0] demultiplexer_3_out0, demultiplexer_3_out1, multiplexer_1_out;

  not not_1 (not_1_out, BUS_SEL);
  Demultiplexer #(.width(16)) demultiplexer_1 (
    .out0(DBUS), .in(demultiplexer_3_out0), .sel(BUS_SEL), .en(not_1_out));  // open: out1
  Demultiplexer #(.width(16)) demultiplexer_2 (
    .out1(ABUS), .in(demultiplexer_3_out1), .sel(BUS_SEL), .en(BUS_SEL));  // open: out0
  Demultiplexer #(.width(16)) demultiplexer_3 (
    .out0(demultiplexer_3_out0), .out1(demultiplexer_3_out1), .in(multiplexer_1_out), .sel(BUS_SEL),
    .en(ENB_OUT));
  Multiplexer #(.width(16), .enable("false")) multiplexer_1 (
    .in0(REGA), .in1(REGB), .out(multiplexer_1_out), .sel(REG_SEL));
endmodule

// ESP / EBP
module RAM_Register (
  input  [15:0] INPUT,
  input  CLK,
  input  _7f_RES,
  input  ff_RES,
  input  [2:0] RAM_REG,
  output [15:0] ABUS,
  output [15:0] DBUS,
  output [7:0] ESP_15_8,
  output [7:0] ESP_7_0,
  output [7:0] EBP_15_8,
  output [7:0] EBP_7_0,
  output CLK_2
);

  wire and_1_out, and_2_out, and_3_out, and_4_out, and_5_out, and_6_out, and_7_out, and_8_out, and_9_out,
       and_10_out, not_1_out, or_1_out, or_2_out, or_3_out, or_4_out, or_5_out, or_6_out, or_7_out;
  wire [15:0] demultiplexer_1_out0, demultiplexer_1_out1, demultiplexer_3_out0, demultiplexer_3_out1,
       multiplexer_1_out, multiplexer_2_out, multiplexer_3_out, rom_1_data;

  or or_1 (or_1_out, _7f_RES, ff_RES);
  ROM #(.addrWidth(2), .dataWidth(16)) rom_1 (.addr({1'b0, _7f_RES}), .data(rom_1_data), .sel(or_1_out));
  Demultiplexer #(.width(16), .enable("false")) demultiplexer_1 (
    .out0(demultiplexer_1_out0), .out1(demultiplexer_1_out1), .in(INPUT), .sel(or_2_out));
  Multiplexer #(.width(16), .enable("false")) multiplexer_1 (
    .in0(demultiplexer_1_out0), .in1(rom_1_data), .out(multiplexer_1_out), .sel(or_1_out));
  Demultiplexer #(.width(16)) demultiplexer_2 (
    .out0(ABUS), .in(demultiplexer_3_out0), .sel(not_1_out), .en(or_4_out));  // open: out1
  Register #(.width(16), .trigger("falling")) ESP (
    .D(multiplexer_2_out), .en(or_2_out), .Q({ESP_15_8, ESP_7_0}), .clk(CLK));  // open: clr
  Multiplexer #(.width(16), .enable("false")) multiplexer_2 (
    .in0(demultiplexer_1_out1), .in1(rom_1_data), .out(multiplexer_2_out), .sel(or_1_out));
  Register #(.width(16), .trigger("falling")) EBP (
    .D(multiplexer_1_out), .en(or_3_out), .Q({EBP_15_8, EBP_7_0}), .clk(CLK));  // open: clr
  or or_2 (or_2_out, or_1_out, and_1_out);
  or or_3 (or_3_out, or_1_out, and_2_out);
  not not_1 (not_1_out, or_4_out);
  Demultiplexer #(.width(16)) demultiplexer_3 (
    .out0(demultiplexer_3_out0), .out1(demultiplexer_3_out1), .in(multiplexer_3_out), .sel(or_6_out),
    .en(or_5_out));
  Multiplexer #(.width(16), .enable("false")) multiplexer_3 (
    .in0({ESP_15_8, ESP_7_0}), .in1({EBP_15_8, EBP_7_0}), .out(multiplexer_3_out), .sel(or_7_out));
  and and_1 (and_1_out, RAM_REG[0], ~RAM_REG[1], RAM_REG[2]);  // AND_Gate
  and and_2 (and_2_out, ~RAM_REG[0], RAM_REG[1], RAM_REG[2]);  // AND_Gate
  Demultiplexer #(.width(16)) demultiplexer_4 (
    .out1(DBUS), .in(demultiplexer_3_out1), .sel(or_6_out), .en(or_6_out));  // open: out0
  or or_4 (or_4_out, and_4_out, and_8_out);
  and and_3 (and_3_out, ~RAM_REG[0], ~RAM_REG[1], RAM_REG[2]);  // AND_Gate
  or or_5 (or_5_out, and_3_out, and_9_out, and_10_out, and_4_out);
  and and_4 (and_4_out, RAM_REG[0], ~RAM_REG[1], ~RAM_REG[2]);  // AND_Gate
  and and_5 (and_5_out, ~RAM_REG[0], ~RAM_REG[1], RAM_REG[2]);  // AND_Gate
  or or_6 (or_6_out, and_5_out, and_6_out);
  and and_6 (and_6_out, RAM_REG[0], RAM_REG[1], ~RAM_REG[2]);  // AND_Gate
  and and_7 (and_7_out, ~RAM_REG[0], ~RAM_REG[1], RAM_REG[2]);  // AND_Gate
  or or_7 (or_7_out, and_7_out, and_8_out);
  and and_8 (and_8_out, ~RAM_REG[0], RAM_REG[1], ~RAM_REG[2]);  // AND_Gate
  and and_9 (and_9_out, RAM_REG[0], RAM_REG[1], ~RAM_REG[2]);  // AND_Gate
  and and_10 (and_10_out, ~RAM_REG[0], RAM_REG[1], ~RAM_REG[2]);  // AND_Gate

  assign CLK_2 = CLK;

  // Notes on the sheet:
  //   contents of rom_1 (hex, n*v repeats v):
  //   ffff 7fff ffff abcd
endmodule

// SHIFT
module ALU_v2_SHIFTER (
  input  [5:0] SHIFT,
  input  [15:0] IN_A,
  output [15:0] OUT_B
);

  wire multiplexer_1_out, multiplexer_2_out, multiplexer_5_out, multiplexer_6_out, multiplexer_7_out,
       multiplexer_8_out, multiplexer_9_out, multiplexer_10_out, multiplexer_13_out, multiplexer_14_out,
       multiplexer_15_out, multiplexer_16_out, multiplexer_17_out, multiplexer_18_out, multiplexer_21_out,
       multiplexer_22_out, multiplexer_23_out, multiplexer_24_out, multiplexer_25_out, multiplexer_26_out,
       multiplexer_29_out, multiplexer_30_out, multiplexer_31_out, multiplexer_32_out, multiplexer_33_out,
       multiplexer_34_out, multiplexer_35_out, multiplexer_37_out, multiplexer_39_out, multiplexer_40_out,
       multiplexer_41_out, multiplexer_42_out, multiplexer_43_out, multiplexer_45_out, multiplexer_47_out,
       multiplexer_48_out, multiplexer_49_out, multiplexer_50_out, multiplexer_51_out, multiplexer_53_out,
       multiplexer_55_out, multiplexer_56_out, multiplexer_57_out, multiplexer_58_out, multiplexer_60_out,
       multiplexer_62_out, multiplexer_63_out, not_1_out, not_2_out, not_3_out, not_4_out, not_5_out,
       not_6_out, not_7_out, not_8_out;

  Multiplexer #(.select(4), .enable("false")) multiplexer_1 (
    .in0(IN_A[11]), .in1(IN_A[10]), .in2(IN_A[9]), .in3(IN_A[8]), .in4(IN_A[7]), .in5(IN_A[6]),
    .in6(IN_A[5]), .in7(IN_A[4]), .in8(IN_A[3]), .in9(IN_A[2]), .in10(IN_A[1]), .in11(IN_A[0]), .in12(1'b0),
    .in13(1'b0), .in14(1'b0), .in15(1'b0), .out(multiplexer_1_out), .sel(SHIFT[4:1]));
  Multiplexer #(.select(4), .enable("false")) multiplexer_2 (
    .in0(IN_A[15]), .in1(IN_A[14]), .in2(IN_A[13]), .in3(IN_A[12]), .in4(IN_A[11]), .in5(IN_A[10]),
    .in6(IN_A[9]), .in7(IN_A[8]), .in8(IN_A[7]), .in9(IN_A[6]), .in10(IN_A[5]), .in11(IN_A[4]),
    .in12(IN_A[3]), .in13(IN_A[2]), .in14(IN_A[1]), .in15(IN_A[0]), .out(multiplexer_2_out), .sel(SHIFT[4:1]));
  not not_1 (not_1_out, SHIFT[5]);
  Multiplexer #(.enable("false")) multiplexer_3 (
    .in0(multiplexer_1_out), .in1(multiplexer_6_out), .out(OUT_B[11]), .sel(not_1_out));
  not not_2 (not_2_out, SHIFT[5]);
  Multiplexer #(.enable("false")) multiplexer_4 (
    .in0(multiplexer_2_out), .in1(multiplexer_8_out), .out(OUT_B[15]), .sel(not_2_out));
  Multiplexer #(.enable("false")) multiplexer_5 (.in0(1'b0), .in1(IN_A[15]), .out(multiplexer_5_out), .sel(SHIFT[0]));
  Multiplexer #(.select(4), .enable("false")) multiplexer_6 (
    .in0(IN_A[11]), .in1(IN_A[12]), .in2(IN_A[13]), .in3(IN_A[14]), .in4(IN_A[15]), .in5(multiplexer_5_out),
    .in6(multiplexer_5_out), .in7(multiplexer_5_out), .in8(multiplexer_5_out), .in9(multiplexer_5_out),
    .in10(multiplexer_5_out), .in11(multiplexer_5_out), .in12(multiplexer_5_out), .in13(multiplexer_5_out),
    .in14(multiplexer_5_out), .in15(multiplexer_5_out), .out(multiplexer_6_out), .sel(SHIFT[4:1]));
  Multiplexer #(.enable("false")) multiplexer_7 (.in0(1'b0), .in1(IN_A[15]), .out(multiplexer_7_out), .sel(SHIFT[0]));
  Multiplexer #(.select(4), .enable("false")) multiplexer_8 (
    .in0(IN_A[15]), .in1(multiplexer_7_out), .in2(multiplexer_7_out), .in3(multiplexer_7_out),
    .in4(multiplexer_7_out), .in5(multiplexer_7_out), .in6(multiplexer_7_out), .in7(multiplexer_7_out),
    .in8(multiplexer_7_out), .in9(multiplexer_7_out), .in10(multiplexer_7_out), .in11(multiplexer_7_out),
    .in12(multiplexer_7_out), .in13(multiplexer_7_out), .in14(multiplexer_7_out), .in15(multiplexer_7_out),
    .out(multiplexer_8_out), .sel(SHIFT[4:1]));
  Multiplexer #(.select(4), .enable("false")) multiplexer_9 (
    .in0(IN_A[10]), .in1(IN_A[9]), .in2(IN_A[8]), .in3(IN_A[7]), .in4(IN_A[6]), .in5(IN_A[5]), .in6(IN_A[4]),
    .in7(IN_A[3]), .in8(IN_A[2]), .in9(IN_A[1]), .in10(IN_A[0]), .in11(1'b0), .in12(1'b0), .in13(1'b0),
    .in14(1'b0), .in15(1'b0), .out(multiplexer_9_out), .sel(SHIFT[4:1]));
  Multiplexer #(.select(4), .enable("false")) multiplexer_10 (
    .in0(IN_A[14]), .in1(IN_A[13]), .in2(IN_A[12]), .in3(IN_A[11]), .in4(IN_A[10]), .in5(IN_A[9]),
    .in6(IN_A[8]), .in7(IN_A[7]), .in8(IN_A[6]), .in9(IN_A[5]), .in10(IN_A[4]), .in11(IN_A[3]),
    .in12(IN_A[2]), .in13(IN_A[1]), .in14(IN_A[0]), .in15(1'b0), .out(multiplexer_10_out), .sel(SHIFT[4:1]));
  not not_3 (not_3_out, SHIFT[5]);
  Multiplexer #(.enable("false")) multiplexer_11 (
    .in0(multiplexer_9_out), .in1(multiplexer_13_out), .out(OUT_B[10]), .sel(not_3_out));
  not not_4 (not_4_out, SHIFT[5]);
  Multiplexer #(.enable("false")) multiplexer_12 (
    .in0(multiplexer_10_out), .in1(multiplexer_14_out), .out(OUT_B[14]), .sel(not_4_out));
  Multiplexer #(.select(4), .enable("false")) multiplexer_13 (
    .in0(IN_A[10]), .in1(IN_A[11]), .in2(IN_A[12]), .in3(IN_A[13]), .in4(IN_A[14]), .in5(IN_A[15]),
    .in6(multiplexer_15_out), .in7(multiplexer_15_out), .in8(multiplexer_15_out), .in9(multiplexer_15_out),
    .in10(multiplexer_15_out), .in11(multiplexer_15_out), .in12(multiplexer_15_out),
    .in13(multiplexer_15_out), .in14(multiplexer_15_out), .in15(multiplexer_15_out),
    .out(multiplexer_13_out), .sel(SHIFT[4:1]));
  Multiplexer #(.select(4), .enable("false")) multiplexer_14 (
    .in0(IN_A[14]), .in1(IN_A[15]), .in2(multiplexer_16_out), .in3(multiplexer_16_out),
    .in4(multiplexer_16_out), .in5(multiplexer_16_out), .in6(multiplexer_16_out), .in7(multiplexer_16_out),
    .in8(multiplexer_16_out), .in9(multiplexer_16_out), .in10(multiplexer_16_out), .in11(multiplexer_16_out),
    .in12(multiplexer_16_out), .in13(multiplexer_16_out), .in14(multiplexer_16_out),
    .in15(multiplexer_16_out), .out(multiplexer_14_out), .sel(SHIFT[4:1]));
  Multiplexer #(.enable("false")) multiplexer_15 (.in0(1'b0), .in1(IN_A[15]), .out(multiplexer_15_out), .sel(SHIFT[0]));
  Multiplexer #(.enable("false")) multiplexer_16 (.in0(1'b0), .in1(IN_A[15]), .out(multiplexer_16_out), .sel(SHIFT[0]));
  Multiplexer #(.select(4), .enable("false")) multiplexer_17 (
    .in0(IN_A[9]), .in1(IN_A[8]), .in2(IN_A[7]), .in3(IN_A[6]), .in4(IN_A[5]), .in5(IN_A[4]), .in6(IN_A[3]),
    .in7(IN_A[2]), .in8(IN_A[1]), .in9(IN_A[0]), .in10(1'b0), .in11(1'b0), .in12(1'b0), .in13(1'b0),
    .in14(1'b0), .in15(1'b0), .out(multiplexer_17_out), .sel(SHIFT[4:1]));
  Multiplexer #(.select(4), .enable("false")) multiplexer_18 (
    .in0(IN_A[13]), .in1(IN_A[12]), .in2(IN_A[11]), .in3(IN_A[10]), .in4(IN_A[9]), .in5(IN_A[8]),
    .in6(IN_A[7]), .in7(IN_A[6]), .in8(IN_A[5]), .in9(IN_A[4]), .in10(IN_A[3]), .in11(IN_A[2]),
    .in12(IN_A[1]), .in13(IN_A[0]), .in14(1'b0), .in15(1'b0), .out(multiplexer_18_out), .sel(SHIFT[4:1]));
  not not_5 (not_5_out, SHIFT[5]);
  Multiplexer #(.enable("false")) multiplexer_19 (
    .in0(multiplexer_17_out), .in1(multiplexer_22_out), .out(OUT_B[9]), .sel(not_5_out));
  not not_6 (not_6_out, SHIFT[5]);
  Multiplexer #(.enable("false")) multiplexer_20 (
    .in0(multiplexer_18_out), .in1(multiplexer_24_out), .out(OUT_B[13]), .sel(not_6_out));
  Multiplexer #(.enable("false")) multiplexer_21 (.in0(1'b0), .in1(IN_A[15]), .out(multiplexer_21_out), .sel(SHIFT[0]));
  Multiplexer #(.select(4), .enable("false")) multiplexer_22 (
    .in0(IN_A[9]), .in1(IN_A[10]), .in2(IN_A[11]), .in3(IN_A[12]), .in4(IN_A[13]), .in5(IN_A[14]),
    .in6(IN_A[15]), .in7(multiplexer_21_out), .in8(multiplexer_21_out), .in9(multiplexer_21_out),
    .in10(multiplexer_21_out), .in11(multiplexer_21_out), .in12(multiplexer_21_out),
    .in13(multiplexer_21_out), .in14(multiplexer_21_out), .in15(multiplexer_21_out),
    .out(multiplexer_22_out), .sel(SHIFT[4:1]));
  Multiplexer #(.enable("false")) multiplexer_23 (.in0(1'b0), .in1(IN_A[15]), .out(multiplexer_23_out), .sel(SHIFT[0]));
  Multiplexer #(.select(4), .enable("false")) multiplexer_24 (
    .in0(IN_A[13]), .in1(IN_A[14]), .in2(IN_A[15]), .in3(multiplexer_23_out), .in4(multiplexer_23_out),
    .in5(multiplexer_23_out), .in6(multiplexer_23_out), .in7(multiplexer_23_out), .in8(multiplexer_23_out),
    .in9(multiplexer_23_out), .in10(multiplexer_23_out), .in11(multiplexer_23_out),
    .in12(multiplexer_23_out), .in13(multiplexer_23_out), .in14(multiplexer_23_out),
    .in15(multiplexer_23_out), .out(multiplexer_24_out), .sel(SHIFT[4:1]));
  Multiplexer #(.select(4), .enable("false")) multiplexer_25 (
    .in0(IN_A[8]), .in1(IN_A[7]), .in2(IN_A[6]), .in3(IN_A[5]), .in4(IN_A[4]), .in5(IN_A[3]), .in6(IN_A[2]),
    .in7(IN_A[1]), .in8(IN_A[0]), .in9(1'b0), .in10(1'b0), .in11(1'b0), .in12(1'b0), .in13(1'b0),
    .in14(1'b0), .in15(1'b0), .out(multiplexer_25_out), .sel(SHIFT[4:1]));
  Multiplexer #(.select(4), .enable("false")) multiplexer_26 (
    .in0(IN_A[12]), .in1(IN_A[11]), .in2(IN_A[10]), .in3(IN_A[9]), .in4(IN_A[8]), .in5(IN_A[7]),
    .in6(IN_A[6]), .in7(IN_A[5]), .in8(IN_A[4]), .in9(IN_A[3]), .in10(IN_A[2]), .in11(IN_A[1]),
    .in12(IN_A[0]), .in13(1'b0), .in14(1'b0), .in15(1'b0), .out(multiplexer_26_out), .sel(SHIFT[4:1]));
  not not_7 (not_7_out, SHIFT[5]);
  Multiplexer #(.enable("false")) multiplexer_27 (
    .in0(multiplexer_25_out), .in1(multiplexer_29_out), .out(OUT_B[8]), .sel(not_7_out));
  not not_8 (not_8_out, SHIFT[5]);
  Multiplexer #(.enable("false")) multiplexer_28 (
    .in0(multiplexer_26_out), .in1(multiplexer_30_out), .out(OUT_B[12]), .sel(not_8_out));
  Multiplexer #(.select(4), .enable("false")) multiplexer_29 (
    .in0(IN_A[8]), .in1(IN_A[9]), .in2(IN_A[10]), .in3(IN_A[11]), .in4(IN_A[12]), .in5(IN_A[13]),
    .in6(IN_A[14]), .in7(IN_A[15]), .in8(multiplexer_31_out), .in9(multiplexer_31_out),
    .in10(multiplexer_31_out), .in11(multiplexer_31_out), .in12(multiplexer_31_out),
    .in13(multiplexer_31_out), .in14(multiplexer_31_out), .in15(multiplexer_31_out),
    .out(multiplexer_29_out), .sel(SHIFT[4:1]));
  Multiplexer #(.select(4), .enable("false")) multiplexer_30 (
    .in0(IN_A[12]), .in1(IN_A[13]), .in2(IN_A[14]), .in3(IN_A[15]), .in4(multiplexer_32_out),
    .in5(multiplexer_32_out), .in6(multiplexer_32_out), .in7(multiplexer_32_out), .in8(multiplexer_32_out),
    .in9(multiplexer_32_out), .in10(multiplexer_32_out), .in11(multiplexer_32_out),
    .in12(multiplexer_32_out), .in13(multiplexer_32_out), .in14(multiplexer_32_out),
    .in15(multiplexer_32_out), .out(multiplexer_30_out), .sel(SHIFT[4:1]));
  Multiplexer #(.enable("false")) multiplexer_31 (.in0(1'b0), .in1(IN_A[15]), .out(multiplexer_31_out), .sel(SHIFT[0]));
  Multiplexer #(.enable("false")) multiplexer_32 (.in0(1'b0), .in1(IN_A[15]), .out(multiplexer_32_out), .sel(SHIFT[0]));
  Multiplexer #(.select(4), .enable("false")) multiplexer_33 (
    .in0(IN_A[3]), .in1(IN_A[4]), .in2(IN_A[5]), .in3(IN_A[6]), .in4(IN_A[7]), .in5(IN_A[8]), .in6(IN_A[9]),
    .in7(IN_A[10]), .in8(IN_A[11]), .in9(IN_A[12]), .in10(IN_A[13]), .in11(IN_A[14]), .in12(IN_A[15]),
    .in13(multiplexer_35_out), .in14(multiplexer_35_out), .in15(multiplexer_35_out),
    .out(multiplexer_33_out), .sel(SHIFT[4:1]));
  Multiplexer #(.select(4), .enable("false")) multiplexer_34 (
    .in0(IN_A[7]), .in1(IN_A[8]), .in2(IN_A[9]), .in3(IN_A[10]), .in4(IN_A[11]), .in5(IN_A[12]),
    .in6(IN_A[13]), .in7(IN_A[14]), .in8(IN_A[15]), .in9(multiplexer_37_out), .in10(multiplexer_37_out),
    .in11(multiplexer_37_out), .in12(multiplexer_37_out), .in13(multiplexer_37_out),
    .in14(multiplexer_37_out), .in15(multiplexer_37_out), .out(multiplexer_34_out), .sel(SHIFT[4:1]));
  Multiplexer #(.enable("false")) multiplexer_35 (.in0(1'b0), .in1(IN_A[15]), .out(multiplexer_35_out), .sel(SHIFT[0]));
  Multiplexer #(.enable("false")) multiplexer_36 (
    .in0(multiplexer_33_out), .in1(multiplexer_39_out), .out(OUT_B[3]), .sel(SHIFT[5]));
  Multiplexer #(.enable("false")) multiplexer_37 (.in0(1'b0), .in1(IN_A[15]), .out(multiplexer_37_out), .sel(SHIFT[0]));
  Multiplexer #(.enable("false")) multiplexer_38 (
    .in0(multiplexer_34_out), .in1(multiplexer_40_out), .out(OUT_B[7]), .sel(SHIFT[5]));
  Multiplexer #(.select(4), .enable("false")) multiplexer_39 (
    .in0(IN_A[3]), .in1(IN_A[2]), .in2(IN_A[1]), .in3(IN_A[0]), .in4(1'b0), .in5(1'b0), .in6(1'b0),
    .in7(1'b0), .in8(1'b0), .in9(1'b0), .in10(1'b0), .in11(1'b0), .in12(1'b0), .in13(1'b0), .in14(1'b0),
    .in15(1'b0), .out(multiplexer_39_out), .sel(SHIFT[4:1]));
  Multiplexer #(.select(4), .enable("false")) multiplexer_40 (
    .in0(IN_A[7]), .in1(IN_A[6]), .in2(IN_A[5]), .in3(IN_A[4]), .in4(IN_A[3]), .in5(IN_A[2]), .in6(IN_A[1]),
    .in7(IN_A[0]), .in8(1'b0), .in9(1'b0), .in10(1'b0), .in11(1'b0), .in12(1'b0), .in13(1'b0), .in14(1'b0),
    .in15(1'b0), .out(multiplexer_40_out), .sel(SHIFT[4:1]));
  Multiplexer #(.select(4), .enable("false")) multiplexer_41 (
    .in0(IN_A[2]), .in1(IN_A[3]), .in2(IN_A[4]), .in3(IN_A[5]), .in4(IN_A[6]), .in5(IN_A[7]), .in6(IN_A[8]),
    .in7(IN_A[9]), .in8(IN_A[10]), .in9(IN_A[11]), .in10(IN_A[12]), .in11(IN_A[13]), .in12(IN_A[14]),
    .in13(IN_A[15]), .in14(multiplexer_43_out), .in15(multiplexer_43_out), .out(multiplexer_41_out),
    .sel(SHIFT[4:1]));
  Multiplexer #(.select(4), .enable("false")) multiplexer_42 (
    .in0(IN_A[6]), .in1(IN_A[7]), .in2(IN_A[8]), .in3(IN_A[9]), .in4(IN_A[10]), .in5(IN_A[11]),
    .in6(IN_A[12]), .in7(IN_A[13]), .in8(IN_A[14]), .in9(IN_A[15]), .in10(multiplexer_45_out),
    .in11(multiplexer_45_out), .in12(multiplexer_45_out), .in13(multiplexer_45_out),
    .in14(multiplexer_45_out), .in15(multiplexer_45_out), .out(multiplexer_42_out), .sel(SHIFT[4:1]));
  Multiplexer #(.enable("false")) multiplexer_43 (.in0(1'b0), .in1(IN_A[15]), .out(multiplexer_43_out), .sel(SHIFT[0]));
  Multiplexer #(.enable("false")) multiplexer_44 (
    .in0(multiplexer_41_out), .in1(multiplexer_47_out), .out(OUT_B[2]), .sel(SHIFT[5]));
  Multiplexer #(.enable("false")) multiplexer_45 (.in0(1'b0), .in1(IN_A[15]), .out(multiplexer_45_out), .sel(SHIFT[0]));
  Multiplexer #(.enable("false")) multiplexer_46 (
    .in0(multiplexer_42_out), .in1(multiplexer_48_out), .out(OUT_B[6]), .sel(SHIFT[5]));
  Multiplexer #(.select(4), .enable("false")) multiplexer_47 (
    .in0(IN_A[2]), .in1(IN_A[1]), .in2(IN_A[0]), .in3(1'b0), .in4(1'b0), .in5(1'b0), .in6(1'b0), .in7(1'b0),
    .in8(1'b0), .in9(1'b0), .in10(1'b0), .in11(1'b0), .in12(1'b0), .in13(1'b0), .in14(1'b0), .in15(1'b0),
    .out(multiplexer_47_out), .sel(SHIFT[4:1]));
  Multiplexer #(.select(4), .enable("false")) multiplexer_48 (
    .in0(IN_A[6]), .in1(IN_A[5]), .in2(IN_A[4]), .in3(IN_A[3]), .in4(IN_A[2]), .in5(IN_A[1]), .in6(IN_A[0]),
    .in7(1'b0), .in8(1'b0), .in9(1'b0), .in10(1'b0), .in11(1'b0), .in12(1'b0), .in13(1'b0), .in14(1'b0),
    .in15(1'b0), .out(multiplexer_48_out), .sel(SHIFT[4:1]));
  Multiplexer #(.select(4), .enable("false")) multiplexer_49 (
    .in0(IN_A[1]), .in1(IN_A[2]), .in2(IN_A[3]), .in3(IN_A[4]), .in4(IN_A[5]), .in5(IN_A[6]), .in6(IN_A[7]),
    .in7(IN_A[8]), .in8(IN_A[9]), .in9(IN_A[10]), .in10(IN_A[11]), .in11(IN_A[12]), .in12(IN_A[13]),
    .in13(IN_A[14]), .in14(IN_A[15]), .in15(multiplexer_51_out), .out(multiplexer_49_out), .sel(SHIFT[4:1]));
  Multiplexer #(.select(4), .enable("false")) multiplexer_50 (
    .in0(IN_A[5]), .in1(IN_A[6]), .in2(IN_A[7]), .in3(IN_A[8]), .in4(IN_A[9]), .in5(IN_A[10]),
    .in6(IN_A[11]), .in7(IN_A[12]), .in8(IN_A[13]), .in9(IN_A[14]), .in10(IN_A[15]),
    .in11(multiplexer_53_out), .in12(multiplexer_53_out), .in13(multiplexer_53_out),
    .in14(multiplexer_53_out), .in15(multiplexer_53_out), .out(multiplexer_50_out), .sel(SHIFT[4:1]));
  Multiplexer #(.enable("false")) multiplexer_51 (.in0(1'b0), .in1(IN_A[15]), .out(multiplexer_51_out), .sel(SHIFT[0]));
  Multiplexer #(.enable("false")) multiplexer_52 (
    .in0(multiplexer_49_out), .in1(multiplexer_55_out), .out(OUT_B[1]), .sel(SHIFT[5]));
  Multiplexer #(.enable("false")) multiplexer_53 (.in0(1'b0), .in1(IN_A[15]), .out(multiplexer_53_out), .sel(SHIFT[0]));
  Multiplexer #(.enable("false")) multiplexer_54 (
    .in0(multiplexer_50_out), .in1(multiplexer_56_out), .out(OUT_B[5]), .sel(SHIFT[5]));
  Multiplexer #(.select(4), .enable("false")) multiplexer_55 (
    .in0(IN_A[1]), .in1(IN_A[0]), .in2(1'b0), .in3(1'b0), .in4(1'b0), .in5(1'b0), .in6(1'b0), .in7(1'b0),
    .in8(1'b0), .in9(1'b0), .in10(1'b0), .in11(1'b0), .in12(1'b0), .in13(1'b0), .in14(1'b0), .in15(1'b0),
    .out(multiplexer_55_out), .sel(SHIFT[4:1]));
  Multiplexer #(.select(4), .enable("false")) multiplexer_56 (
    .in0(IN_A[5]), .in1(IN_A[4]), .in2(IN_A[3]), .in3(IN_A[2]), .in4(IN_A[1]), .in5(IN_A[0]), .in6(1'b0),
    .in7(1'b0), .in8(1'b0), .in9(1'b0), .in10(1'b0), .in11(1'b0), .in12(1'b0), .in13(1'b0), .in14(1'b0),
    .in15(1'b0), .out(multiplexer_56_out), .sel(SHIFT[4:1]));
  Multiplexer #(.select(4), .enable("false")) multiplexer_57 (
    .in0(IN_A[0]), .in1(IN_A[1]), .in2(IN_A[2]), .in3(IN_A[3]), .in4(IN_A[4]), .in5(IN_A[5]), .in6(IN_A[6]),
    .in7(IN_A[7]), .in8(IN_A[8]), .in9(IN_A[9]), .in10(IN_A[10]), .in11(IN_A[11]), .in12(IN_A[12]),
    .in13(IN_A[13]), .in14(IN_A[14]), .in15(IN_A[15]), .out(multiplexer_57_out), .sel(SHIFT[4:1]));
  Multiplexer #(.select(4), .enable("false")) multiplexer_58 (
    .in0(IN_A[4]), .in1(IN_A[5]), .in2(IN_A[6]), .in3(IN_A[7]), .in4(IN_A[8]), .in5(IN_A[9]), .in6(IN_A[10]),
    .in7(IN_A[11]), .in8(IN_A[12]), .in9(IN_A[13]), .in10(IN_A[14]), .in11(IN_A[15]),
    .in12(multiplexer_60_out), .in13(multiplexer_60_out), .in14(multiplexer_60_out),
    .in15(multiplexer_60_out), .out(multiplexer_58_out), .sel(SHIFT[4:1]));
  Multiplexer #(.enable("false")) multiplexer_59 (
    .in0(multiplexer_57_out), .in1(multiplexer_62_out), .out(OUT_B[0]), .sel(SHIFT[5]));
  Multiplexer #(.enable("false")) multiplexer_60 (.in0(1'b0), .in1(IN_A[15]), .out(multiplexer_60_out), .sel(SHIFT[0]));
  Multiplexer #(.enable("false")) multiplexer_61 (
    .in0(multiplexer_58_out), .in1(multiplexer_63_out), .out(OUT_B[4]), .sel(SHIFT[5]));
  Multiplexer #(.select(4), .enable("false")) multiplexer_62 (
    .in0(IN_A[0]), .in1(1'b0), .in2(1'b0), .in3(1'b0), .in4(1'b0), .in5(1'b0), .in6(1'b0), .in7(1'b0),
    .in8(1'b0), .in9(1'b0), .in10(1'b0), .in11(1'b0), .in12(1'b0), .in13(1'b0), .in14(1'b0), .in15(1'b0),
    .out(multiplexer_62_out), .sel(SHIFT[4:1]));
  Multiplexer #(.select(4), .enable("false")) multiplexer_63 (
    .in0(IN_A[4]), .in1(IN_A[3]), .in2(IN_A[2]), .in3(IN_A[1]), .in4(IN_A[0]), .in5(1'b0), .in6(1'b0),
    .in7(1'b0), .in8(1'b0), .in9(1'b0), .in10(1'b0), .in11(1'b0), .in12(1'b0), .in13(1'b0), .in14(1'b0),
    .in15(1'b0), .out(multiplexer_63_out), .sel(SHIFT[4:1]));

  // Notes on the sheet:
  //   B5 - R/L
  //   B0 - U/SGN
endmodule
